// Logisim project 7seg.circ as structural Verilog
module add3IfGreaterThan4 (
  input  in_1,
  input  in_2,
  input  in_3,
  input  in_4,
  output out_5,
  output out_6,
  output out_7,
  output out_8
);

  wire and_1_out, n4bitadder_1_s0, n4bitadder_1_s1, n4bitadder_1_s2, n4bitadder_1_s3, or_1_out, or_2_out;

  or or_1 (or_1_out, in_3, in_4);
  and and_1 (and_1_out, in_2, or_1_out);
  or or_2 (or_2_out, in_1, and_1_out);
  _4bitAdder u_4bitadder_1 (
    .S0(n4bitadder_1_s0), .S1(n4bitadder_1_s1), .S2(n4bitadder_1_s2), .S3(n4bitadder_1_s3), .in_1(in_1),
    .in_2(in_2), .in_3(in_3), .in_4(in_4));
  Multiplexer multiplexer_1 (.in0(in_1), .in1(n4bitadder_1_s3), .out(out_5), .sel(or_2_out), .en(1'b1));
  Multiplexer multiplexer_2 (.in0(in_2), .in1(n4bitadder_1_s2), .out(out_6), .sel(or_2_out), .en(1'b1));
  Multiplexer multiplexer_3 (.in0(in_3), .in1(n4bitadder_1_s1), .out(out_7), .sel(or_2_out), .en(1'b1));
  Multiplexer multiplexer_4 (.in0(in_4), .in1(n4bitadder_1_s0), .out(out_8), .sel(or_2_out), .en(1'b1));
endmodule
