// Logisim project Arithmetic.circ as structural Verilog: 4 circuits, main circuit main
module main (
  input  in_1,
  input  in_2,
  input  in_3,
  input  in_4,
  input  in_5,
  input  in_6,
  input  in_7,
  input  in_8,
  input  in_9,
  input  in_10,
  input  in_11,
  input  in_12,
  input  in_13,
  input  in_14,
  input  in_15,
  input  in_16
);

  wire undriven, undriven_2, undriven_3, undriven_4, undriven_5, undriven_6, undriven_7, undriven_8;

  lookaheadAdderSubtractor lookaheadaddersubtractor_1 (
    .in_16(undriven), .A7(undriven_2), .A6(undriven_3), .A5(undriven_4), .A4(undriven_5), .A3(undriven_6),
    .A2(undriven_7), .A1(undriven_8));  // open: M, S0, S1, S2, S3, S4, S5, S6, S7, B7, B6, B5, B4, B3, B2, B1, B0, V, Sign
  // lookaheadAdderSubtractor lookaheadaddersubtractor_2: pin names not known

  // Other names for the same wires on the sheet: D0 = in_16; d0_t = in_8; D1 = in_15; d1_t = in_7; D2 = in_14;
  //   d2_t = in_6; D3 = in_13; d3_t = in_5; D4 = in_12; d4_t = in_4; D5 = in_11; d5_t = in_3; D6 = in_10; d6_t = in_2;
  //   D7 = in_9; d7_t = in_1
endmodule

module divider (
  input  in_1,
  input  in_2,
  input  in_3,
  input  in_4,
  input  in_5,
  input  in_6,
  input  in_7,
  input  in_8,
  input  in_9,
  input  in_10,
  input  in_11,
  input  in_12,
  input  in_13,
  input  in_14,
  input  in_15,
  input  in_16,
  output out_17,
  output out_18,
  output out_19,
  output out_20,
  output out_21,
  output out_22,
  output out_23,
  output out_24,
  output out_25,
  output out_26,
  output out_27,
  output out_28,
  output out_29,
  output out_30,
  output out_31,
  output out_32
);

  wire _00, _01, _02, _03, _04, _05, _06, _07, _10, _11, _12, _13, _14, _15, _16, _17, _20, _21, _22, _23,
       _24, _25, _26, _27, _30, _31, _32, _33, _34, _35, _36, _37, _40, _41, _42, _43, _44, _45, _46, _47,
       _50, _51, _52, _53, _54, _55, _56, _57, _60, _61, _62, _63, _64, _65, _66, _67;

  DividerCell dividercell_1 (
    .out_17(out_17), .in_1(1'b0), .in_2(1'b0), .in_4(1'b0), .in_6(1'b0), .in_8(1'b0), .in_10(1'b0),
    .in_12(1'b0), .in_14(in_9), .in_3(in_1), .in_5(in_2), .in_7(in_3), .in_9(in_4), .in_11(in_5),
    .in_13(in_6), .in_15(in_7), .in_16(in_8), .out_18(_07), .out_19(_06), .out_20(_05), .out_21(_04),
    .out_22(_03), .out_23(_02), .out_24(_01), .out_25(_00));
  DividerCell dividercell_2 (
    .out_17(out_18), .in_1(_06), .in_2(_05), .in_4(_04), .in_6(_03), .in_8(_02), .in_10(_01), .in_12(_00),
    .in_14(in_10), .in_3(in_1), .in_5(in_2), .in_7(in_3), .in_9(in_4), .in_11(in_5), .in_13(in_6),
    .in_15(in_7), .in_16(in_8), .out_18(_17), .out_19(_16), .out_20(_15), .out_21(_14), .out_22(_13),
    .out_23(_12), .out_24(_11), .out_25(_10));
  DividerCell dividercell_3 (
    .out_17(out_19), .in_1(_16), .in_2(_15), .in_4(_14), .in_6(_13), .in_8(_12), .in_10(_11), .in_12(_10),
    .in_14(in_11), .in_3(in_1), .in_5(in_2), .in_7(in_3), .in_9(in_4), .in_11(in_5), .in_13(in_6),
    .in_15(in_7), .in_16(in_8), .out_18(_27), .out_19(_26), .out_20(_25), .out_21(_24), .out_22(_23),
    .out_23(_22), .out_24(_21), .out_25(_20));
  DividerCell dividercell_4 (
    .out_17(out_20), .in_1(_26), .in_2(_25), .in_4(_24), .in_6(_23), .in_8(_22), .in_10(_21), .in_12(_20),
    .in_14(in_12), .in_3(in_1), .in_5(in_2), .in_7(in_3), .in_9(in_4), .in_11(in_5), .in_13(in_6),
    .in_15(in_7), .in_16(in_8), .out_18(_37), .out_19(_36), .out_20(_35), .out_21(_34), .out_22(_33),
    .out_23(_32), .out_24(_31), .out_25(_30));
  DividerCell dividercell_5 (
    .out_17(out_21), .in_1(_36), .in_2(_35), .in_4(_34), .in_6(_33), .in_8(_32), .in_10(_31), .in_12(_30),
    .in_14(in_13), .in_3(in_1), .in_5(in_2), .in_7(in_3), .in_9(in_4), .in_11(in_5), .in_13(in_6),
    .in_15(in_7), .in_16(in_8), .out_18(_47), .out_19(_46), .out_20(_45), .out_21(_44), .out_22(_43),
    .out_23(_42), .out_24(_41), .out_25(_40));
  DividerCell dividercell_6 (
    .out_17(out_22), .in_1(_46), .in_2(_45), .in_4(_44), .in_6(_43), .in_8(_42), .in_10(_41), .in_12(_40),
    .in_14(in_14), .in_3(in_1), .in_5(in_2), .in_7(in_3), .in_9(in_4), .in_11(in_5), .in_13(in_6),
    .in_15(in_7), .in_16(in_8), .out_18(_57), .out_19(_56), .out_20(_55), .out_21(_54), .out_22(_53),
    .out_23(_52), .out_24(_51), .out_25(_50));
  DividerCell dividercell_7 (
    .out_17(out_23), .in_1(_56), .in_2(_55), .in_4(_54), .in_6(_53), .in_8(_52), .in_10(_51), .in_12(_50),
    .in_14(in_15), .in_3(in_1), .in_5(in_2), .in_7(in_3), .in_9(in_4), .in_11(in_5), .in_13(in_6),
    .in_15(in_7), .in_16(in_8), .out_18(_67), .out_19(_66), .out_20(_65), .out_21(_64), .out_22(_63),
    .out_23(_62), .out_24(_61), .out_25(_60));
  DividerCell dividercell_8 (
    .out_17(out_24), .in_1(_66), .in_2(_65), .in_4(_64), .in_6(_63), .in_8(_62), .in_10(_61), .in_12(_60),
    .in_14(in_16), .in_3(in_1), .in_5(in_2), .in_7(in_3), .in_9(in_4), .in_11(in_5), .in_13(in_6),
    .in_15(in_7), .in_16(in_8), .out_18(out_25), .out_19(out_26), .out_20(out_27), .out_21(out_28),
    .out_22(out_29), .out_23(out_30), .out_24(out_31), .out_25(out_32));

  // Other names for the same wires on the sheet: D0 = in_16; d0_t = in_8; D1 = in_15; d1_t = in_7; D2 = in_14;
  //   d2_t = in_6; D3 = in_13; d3_t = in_5; D4 = in_12; d4_t = in_4; D5 = in_11; d5_t = in_3; D6 = in_10; d6_t = in_2;
  //   D7 = in_9; d7_t = in_1; Q0 = out_24; Q1 = out_23; Q2 = out_22; Q3 = out_21; Q4 = out_20; Q5 = out_19;
  //   Q6 = out_18; Q7 = out_17; R0 = out_32; R1 = out_31; R2 = out_30; R3 = out_29; R4 = out_28; R5 = out_27;
  //   R6 = out_26; R7 = out_25
endmodule

module RestoreLogic (
  input  in_1,
  input  in_2,
  input  in_3,
  input  in_4,
  input  in_5,
  input  in_6,
  input  in_7,
  input  in_8,
  input  in_9,
  input  in_10,
  input  in_11,
  input  in_12,
  input  in_13,
  input  in_14,
  input  in_15,
  input  in_16,
  input  in_17,
  output out_18,
  output out_19,
  output out_20,
  output out_21,
  output out_22,
  output out_23,
  output out_24,
  output out_25
);

  Multiplexer multiplexer_1 (.in0(in_9), .in1(in_1), .out(out_18), .sel(in_17), .en(1'b1));
  Multiplexer multiplexer_2 (.in0(in_10), .in1(in_2), .out(out_19), .sel(in_17), .en(1'b1));
  Multiplexer multiplexer_3 (.in0(in_11), .in1(in_3), .out(out_20), .sel(in_17), .en(1'b1));
  Multiplexer multiplexer_4 (.in0(in_12), .in1(in_4), .out(out_21), .sel(in_17), .en(1'b1));
  Multiplexer multiplexer_5 (.in0(in_13), .in1(in_5), .out(out_22), .sel(in_17), .en(1'b1));
  Multiplexer multiplexer_6 (.in0(in_15), .in1(in_7), .out(out_24), .sel(in_17), .en(1'b1));
  Multiplexer multiplexer_7 (.in0(in_14), .in1(in_6), .out(out_23), .sel(in_17), .en(1'b1));
  Multiplexer multiplexer_8 (.in0(in_16), .in1(in_8), .out(out_25), .sel(in_17), .en(1'b1));
endmodule

module DividerCell (
  input  in_1,
  input  in_2,
  input  in_3,
  input  in_4,
  input  in_5,
  input  in_6,
  input  in_7,
  input  in_8,
  input  in_9,
  input  in_10,
  input  in_11,
  input  in_12,
  input  in_13,
  input  in_14,
  input  in_15,
  input  in_16,
  output out_17,
  output out_18,
  output out_19,
  output out_20,
  output out_21,
  output out_22,
  output out_23,
  output out_24,
  output out_25
);

  wire lookaheadaddersubtractor_1_s0, lookaheadaddersubtractor_1_s1, lookaheadaddersubtractor_1_s2,
       lookaheadaddersubtractor_1_s3, lookaheadaddersubtractor_1_s4, lookaheadaddersubtractor_1_s5,
       lookaheadaddersubtractor_1_s6, lookaheadaddersubtractor_1_s7;

  RestoreLogic restorelogic_1 (
    .in_17(out_17), .in_9(in_1), .in_10(in_2), .in_11(in_4), .in_12(in_6), .in_13(in_8), .in_14(in_10),
    .in_15(in_12), .in_16(in_14), .in_1(lookaheadaddersubtractor_1_s7), .in_2(lookaheadaddersubtractor_1_s6),
    .in_3(lookaheadaddersubtractor_1_s5), .in_4(lookaheadaddersubtractor_1_s4),
    .in_5(lookaheadaddersubtractor_1_s3), .in_6(lookaheadaddersubtractor_1_s2),
    .in_7(lookaheadaddersubtractor_1_s1), .in_8(lookaheadaddersubtractor_1_s0), .out_18(out_18),
    .out_19(out_19), .out_20(out_20), .out_21(out_21), .out_22(out_22), .out_23(out_23), .out_24(out_24),
    .out_25(out_25));
  lookaheadAdderSubtractor lookaheadaddersubtractor_1 (
    .M(1'b1), .S0(lookaheadaddersubtractor_1_s0), .S1(lookaheadaddersubtractor_1_s1),
    .S2(lookaheadaddersubtractor_1_s2), .S3(lookaheadaddersubtractor_1_s3),
    .S4(lookaheadaddersubtractor_1_s4), .S5(lookaheadaddersubtractor_1_s5),
    .S6(lookaheadaddersubtractor_1_s6), .S7(lookaheadaddersubtractor_1_s7), .in_16(in_1), .A7(in_2),
    .A6(in_4), .A5(in_6), .A4(in_8), .A3(in_10), .A2(in_12), .A1(in_14), .B7(in_3), .B6(in_5), .B5(in_7),
    .B4(in_9), .B3(in_11), .B2(in_13), .B1(in_15), .B0(in_16), .Sign(out_17));  // open: V
endmodule
