// Logisim project Arithmetic1.circ as structural Verilog: 8 circuits, main circuit divider
module divider (
  input  in_1,
  input  in_2,
  input  in_3,
  input  in_4,
  input  in_5,
  input  in_6,
  input  in_7,
  input  in_8,
  input  in_9,
  input  in_10,
  input  in_11,
  input  in_12,
  input  in_13,
  input  in_14,
  input  in_15,
  input  in_16,
  output out_17,
  output out_18,
  output out_19,
  output out_20,
  output out_21,
  output out_22,
  output out_23,
  output out_24,
  output out_25,
  output out_26,
  output out_27,
  output out_28,
  output out_29,
  output out_30,
  output out_31,
  output out_32
);

  wire _00, _01, _02, _03, _04, _05, _06, _07, _10, _11, _12, _13, _14, _15, _16, _17, _20, _21, _22, _23,
       _24, _25, _26, _27, _30, _31, _32, _33, _34, _35, _36, _37, _40, _41, _42, _43, _44, _45, _46, _47,
       _50, _51, _52, _53, _54, _55, _56, _57, _60, _61, _62, _63, _64, _65, _66, _67;

  DividerCell dividercell_1 (
    .out_17(out_17), .in_1(1'b0), .in_2(1'b0), .in_4(1'b0), .in_6(1'b0), .in_8(1'b0), .in_10(1'b0),
    .in_12(1'b0), .in_14(in_9), .in_3(in_1), .in_5(in_2), .in_7(in_3), .in_9(in_4), .in_11(in_5),
    .in_13(in_6), .in_15(in_7), .in_16(in_8), .out_18(_07), .out_19(_06), .out_20(_05), .out_21(_04),
    .out_22(_03), .out_23(_02), .out_24(_01), .out_25(_00));
  DividerCell dividercell_2 (
    .out_17(out_18), .in_1(_06), .in_2(_05), .in_4(_04), .in_6(_03), .in_8(_02), .in_10(_01), .in_12(_00),
    .in_14(in_10), .in_3(in_1), .in_5(in_2), .in_7(in_3), .in_9(in_4), .in_11(in_5), .in_13(in_6),
    .in_15(in_7), .in_16(in_8), .out_18(_17), .out_19(_16), .out_20(_15), .out_21(_14), .out_22(_13),
    .out_23(_12), .out_24(_11), .out_25(_10));
  DividerCell dividercell_3 (
    .out_17(out_19), .in_1(_16), .in_2(_15), .in_4(_14), .in_6(_13), .in_8(_12), .in_10(_11), .in_12(_10),
    .in_14(in_11), .in_3(in_1), .in_5(in_2), .in_7(in_3), .in_9(in_4), .in_11(in_5), .in_13(in_6),
    .in_15(in_7), .in_16(in_8), .out_18(_27), .out_19(_26), .out_20(_25), .out_21(_24), .out_22(_23),
    .out_23(_22), .out_24(_21), .out_25(_20));
  DividerCell dividercell_4 (
    .out_17(out_20), .in_1(_26), .in_2(_25), .in_4(_24), .in_6(_23), .in_8(_22), .in_10(_21), .in_12(_20),
    .in_14(in_12), .in_3(in_1), .in_5(in_2), .in_7(in_3), .in_9(in_4), .in_11(in_5), .in_13(in_6),
    .in_15(in_7), .in_16(in_8), .out_18(_37), .out_19(_36), .out_20(_35), .out_21(_34), .out_22(_33),
    .out_23(_32), .out_24(_31), .out_25(_30));
  DividerCell dividercell_5 (
    .out_17(out_21), .in_1(_36), .in_2(_35), .in_4(_34), .in_6(_33), .in_8(_32), .in_10(_31), .in_12(_30),
    .in_14(in_13), .in_3(in_1), .in_5(in_2), .in_7(in_3), .in_9(in_4), .in_11(in_5), .in_13(in_6),
    .in_15(in_7), .in_16(in_8), .out_18(_47), .out_19(_46), .out_20(_45), .out_21(_44), .out_22(_43),
    .out_23(_42), .out_24(_41), .out_25(_40));
  DividerCell dividercell_6 (
    .out_17(out_22), .in_1(_46), .in_2(_45), .in_4(_44), .in_6(_43), .in_8(_42), .in_10(_41), .in_12(_40),
    .in_14(in_14), .in_3(in_1), .in_5(in_2), .in_7(in_3), .in_9(in_4), .in_11(in_5), .in_13(in_6),
    .in_15(in_7), .in_16(in_8), .out_18(_57), .out_19(_56), .out_20(_55), .out_21(_54), .out_22(_53),
    .out_23(_52), .out_24(_51), .out_25(_50));
  DividerCell dividercell_7 (
    .out_17(out_23), .in_1(_56), .in_2(_55), .in_4(_54), .in_6(_53), .in_8(_52), .in_10(_51), .in_12(_50),
    .in_14(in_15), .in_3(in_1), .in_5(in_2), .in_7(in_3), .in_9(in_4), .in_11(in_5), .in_13(in_6),
    .in_15(in_7), .in_16(in_8), .out_18(_67), .out_19(_66), .out_20(_65), .out_21(_64), .out_22(_63),
    .out_23(_62), .out_24(_61), .out_25(_60));
  DividerCell dividercell_8 (
    .out_17(out_24), .in_1(_66), .in_2(_65), .in_4(_64), .in_6(_63), .in_8(_62), .in_10(_61), .in_12(_60),
    .in_14(in_16), .in_3(in_1), .in_5(in_2), .in_7(in_3), .in_9(in_4), .in_11(in_5), .in_13(in_6),
    .in_15(in_7), .in_16(in_8), .out_18(out_25), .out_19(out_26), .out_20(out_27), .out_21(out_28),
    .out_22(out_29), .out_23(out_30), .out_24(out_31), .out_25(out_32));

  // Other names for the same wires on the sheet: D0 = in_16; d0_t = in_8; D1 = in_15; d1_t = in_7; D2 = in_14;
  //   d2_t = in_6; D3 = in_13; d3_t = in_5; D4 = in_12; d4_t = in_4; D5 = in_11; d5_t = in_3; D6 = in_10; d6_t = in_2;
  //   D7 = in_9; d7_t = in_1; Q0 = out_24; Q1 = out_23; Q2 = out_22; Q3 = out_21; Q4 = out_20; Q5 = out_19;
  //   Q6 = out_18; Q7 = out_17; R0 = out_32; R1 = out_31; R2 = out_30; R3 = out_29; R4 = out_28; R5 = out_27;
  //   R6 = out_26; R7 = out_25
endmodule

module RestoreLogic (
  input  in_1,
  input  in_2,
  input  in_3,
  input  in_4,
  input  in_5,
  input  in_6,
  input  in_7,
  input  in_8,
  input  in_9,
  input  in_10,
  input  in_11,
  input  in_12,
  input  in_13,
  input  in_14,
  input  in_15,
  input  in_16,
  input  in_17,
  output out_18,
  output out_19,
  output out_20,
  output out_21,
  output out_22,
  output out_23,
  output out_24,
  output out_25
);

  Multiplexer multiplexer_1 (.in0(in_9), .in1(in_1), .out(out_18), .sel(in_17), .en(1'b1));
  Multiplexer multiplexer_2 (.in0(in_11), .in1(in_3), .out(out_20), .sel(in_17), .en(1'b1));
  Multiplexer multiplexer_3 (.in0(in_10), .in1(in_2), .out(out_19), .sel(in_17), .en(1'b1));
  Multiplexer multiplexer_4 (.in0(in_12), .in1(in_4), .out(out_21), .sel(in_17), .en(1'b1));
  Multiplexer multiplexer_5 (.in0(in_13), .in1(in_5), .out(out_22), .sel(in_17), .en(1'b1));
  Multiplexer multiplexer_6 (.in0(in_15), .in1(in_7), .out(out_24), .sel(in_17), .en(1'b1));
  Multiplexer multiplexer_7 (.in0(in_14), .in1(in_6), .out(out_23), .sel(in_17), .en(1'b1));
  Multiplexer multiplexer_8 (.in0(in_16), .in1(in_8), .out(out_25), .sel(in_17), .en(1'b1));
endmodule

module DividerCell (
  input  in_1,
  input  in_2,
  input  in_3,
  input  in_4,
  input  in_5,
  input  in_6,
  input  in_7,
  input  in_8,
  input  in_9,
  input  in_10,
  input  in_11,
  input  in_12,
  input  in_13,
  input  in_14,
  input  in_15,
  input  in_16,
  output out_17,
  output out_18,
  output out_19,
  output out_20,
  output out_21,
  output out_22,
  output out_23,
  output out_24,
  output out_25
);

  wire lookaheadaddersubtractor_1_s0, lookaheadaddersubtractor_1_s1, lookaheadaddersubtractor_1_s2,
       lookaheadaddersubtractor_1_s3, lookaheadaddersubtractor_1_s4, lookaheadaddersubtractor_1_s5,
       lookaheadaddersubtractor_1_s6, lookaheadaddersubtractor_1_s7;

  RestoreLogic restorelogic_1 (
    .in_17(out_17), .in_9(in_1), .in_10(in_2), .in_11(in_4), .in_12(in_6), .in_13(in_8), .in_14(in_10),
    .in_15(in_12), .in_16(in_14), .in_1(lookaheadaddersubtractor_1_s7), .in_2(lookaheadaddersubtractor_1_s6),
    .in_3(lookaheadaddersubtractor_1_s5), .in_4(lookaheadaddersubtractor_1_s4),
    .in_5(lookaheadaddersubtractor_1_s3), .in_6(lookaheadaddersubtractor_1_s2),
    .in_7(lookaheadaddersubtractor_1_s1), .in_8(lookaheadaddersubtractor_1_s0), .out_18(out_18),
    .out_19(out_19), .out_20(out_20), .out_21(out_21), .out_22(out_22), .out_23(out_23), .out_24(out_24),
    .out_25(out_25));
  lookaheadAdderSubtractor lookaheadaddersubtractor_1 (
    .M(1'b1), .S0(lookaheadaddersubtractor_1_s0), .S1(lookaheadaddersubtractor_1_s1),
    .S2(lookaheadaddersubtractor_1_s2), .S3(lookaheadaddersubtractor_1_s3),
    .S4(lookaheadaddersubtractor_1_s4), .S5(lookaheadaddersubtractor_1_s5),
    .S6(lookaheadaddersubtractor_1_s6), .S7(lookaheadaddersubtractor_1_s7), .in_16(in_1), .A7(in_2),
    .A6(in_4), .A5(in_6), .A4(in_8), .A3(in_10), .A2(in_12), .A1(in_14), .B7(in_3), .B6(in_5), .B5(in_7),
    .B4(in_9), .B3(in_11), .B2(in_13), .B1(in_15), .B0(in_16), .Sign(out_17));  // open: V
endmodule

module binToBcd (
  input  in_1,
  input  in_2,
  input  in_3,
  input  in_4,
  input  in_5,
  input  in_6,
  input  in_7,
  input  in_8,
  input  in_9,
  input  in_10,
  input  in_11,
  input  in_12,
  input  in_13,
  input  in_14,
  input  in_15,
  input  in_16,
  output out_17,
  output out_18,
  output out_19,
  output out_20,
  output out_21,
  output out_22,
  output out_23,
  output out_24,
  output out_25,
  output out_26,
  output out_27,
  output out_28,
  output out_29,
  output out_30,
  output out_31,
  output out_32,
  output out_33,
  output out_34,
  output out_35,
  output out_36,
  output out_37
);

  wire add3ifgreaterthan4_1_out_6, add3ifgreaterthan4_1_out_7, add3ifgreaterthan4_1_out_8,
       add3ifgreaterthan4_2_out_6, add3ifgreaterthan4_2_out_7, add3ifgreaterthan4_2_out_8,
       add3ifgreaterthan4_4_out_6, add3ifgreaterthan4_4_out_7, add3ifgreaterthan4_4_out_8,
       add3ifgreaterthan4_5_out_6, add3ifgreaterthan4_5_out_7, add3ifgreaterthan4_5_out_8,
       add3ifgreaterthan4_6_out_5, add3ifgreaterthan4_6_out_6, add3ifgreaterthan4_6_out_7,
       add3ifgreaterthan4_6_out_8, add3ifgreaterthan4_7_out_5, add3ifgreaterthan4_7_out_6,
       add3ifgreaterthan4_7_out_7, add3ifgreaterthan4_7_out_8, add3ifgreaterthan4_8_out_5,
       add3ifgreaterthan4_8_out_6, add3ifgreaterthan4_8_out_7, add3ifgreaterthan4_8_out_8,
       add3ifgreaterthan4_9_out_5, add3ifgreaterthan4_9_out_6, add3ifgreaterthan4_9_out_7,
       add3ifgreaterthan4_9_out_8, add3ifgreaterthan4_10_out_5, add3ifgreaterthan4_10_out_6,
       add3ifgreaterthan4_10_out_7, add3ifgreaterthan4_10_out_8, add3ifgreaterthan4_11_out_5,
       add3ifgreaterthan4_11_out_6, add3ifgreaterthan4_11_out_7, add3ifgreaterthan4_11_out_8,
       add3ifgreaterthan4_12_out_5, add3ifgreaterthan4_12_out_6, add3ifgreaterthan4_12_out_7,
       add3ifgreaterthan4_12_out_8, add3ifgreaterthan4_13_out_5, add3ifgreaterthan4_13_out_6,
       add3ifgreaterthan4_13_out_7, add3ifgreaterthan4_13_out_8, add3ifgreaterthan4_14_out_5,
       add3ifgreaterthan4_14_out_6, add3ifgreaterthan4_14_out_7, add3ifgreaterthan4_14_out_8,
       add3ifgreaterthan4_16_out_5, add3ifgreaterthan4_16_out_6, add3ifgreaterthan4_16_out_7,
       add3ifgreaterthan4_16_out_8, add3ifgreaterthan4_17_out_5, add3ifgreaterthan4_17_out_6,
       add3ifgreaterthan4_17_out_7, add3ifgreaterthan4_17_out_8, add3ifgreaterthan4_18_out_5,
       add3ifgreaterthan4_18_out_6, add3ifgreaterthan4_18_out_7, add3ifgreaterthan4_18_out_8,
       add3ifgreaterthan4_19_out_5, add3ifgreaterthan4_19_out_6, add3ifgreaterthan4_19_out_7,
       add3ifgreaterthan4_19_out_8, add3ifgreaterthan4_20_out_5, add3ifgreaterthan4_20_out_6,
       add3ifgreaterthan4_20_out_7, add3ifgreaterthan4_20_out_8, add3ifgreaterthan4_21_out_5,
       add3ifgreaterthan4_21_out_6, add3ifgreaterthan4_21_out_7, add3ifgreaterthan4_21_out_8,
       add3ifgreaterthan4_22_out_5, add3ifgreaterthan4_22_out_6, add3ifgreaterthan4_22_out_7,
       add3ifgreaterthan4_22_out_8, add3ifgreaterthan4_23_out_5, add3ifgreaterthan4_23_out_6,
       add3ifgreaterthan4_23_out_7, add3ifgreaterthan4_23_out_8, add3ifgreaterthan4_24_out_5,
       add3ifgreaterthan4_24_out_6, add3ifgreaterthan4_24_out_7, add3ifgreaterthan4_24_out_8,
       add3ifgreaterthan4_25_out_5, add3ifgreaterthan4_25_out_6, add3ifgreaterthan4_25_out_7,
       add3ifgreaterthan4_25_out_8, add3ifgreaterthan4_27_out_5, add3ifgreaterthan4_27_out_6,
       add3ifgreaterthan4_27_out_7, add3ifgreaterthan4_27_out_8, add3ifgreaterthan4_28_out_5,
       add3ifgreaterthan4_28_out_6, add3ifgreaterthan4_28_out_7, add3ifgreaterthan4_28_out_8,
       add3ifgreaterthan4_29_out_5, add3ifgreaterthan4_29_out_6, add3ifgreaterthan4_29_out_7,
       add3ifgreaterthan4_29_out_8, add3ifgreaterthan4_30_out_5, add3ifgreaterthan4_30_out_6,
       add3ifgreaterthan4_30_out_7, add3ifgreaterthan4_30_out_8, add3ifgreaterthan4_31_out_5,
       add3ifgreaterthan4_31_out_6, add3ifgreaterthan4_31_out_7, add3ifgreaterthan4_31_out_8,
       add3ifgreaterthan4_32_out_5, add3ifgreaterthan4_32_out_6, add3ifgreaterthan4_32_out_7,
       add3ifgreaterthan4_32_out_8, add3ifgreaterthan4_34_out_5, add3ifgreaterthan4_34_out_6,
       add3ifgreaterthan4_34_out_7, add3ifgreaterthan4_34_out_8, add3ifgreaterthan4_35_out_5,
       add3ifgreaterthan4_35_out_6, add3ifgreaterthan4_35_out_7, add3ifgreaterthan4_35_out_8;

  add3IfGreaterThan4 add3ifgreaterthan4_1 (
    .in_1(add3ifgreaterthan4_2_out_6), .in_2(add3ifgreaterthan4_2_out_7), .in_3(add3ifgreaterthan4_2_out_8),
    .in_4(add3ifgreaterthan4_7_out_5), .out_5(out_18), .out_6(add3ifgreaterthan4_1_out_6),
    .out_7(add3ifgreaterthan4_1_out_7), .out_8(add3ifgreaterthan4_1_out_8));
  add3IfGreaterThan4 add3ifgreaterthan4_2 (
    .in_1(1'b0), .in_2(1'b0), .in_3(add3ifgreaterthan4_9_out_5), .in_4(add3ifgreaterthan4_8_out_5),
    .out_5(out_17), .out_6(add3ifgreaterthan4_2_out_6), .out_7(add3ifgreaterthan4_2_out_7),
    .out_8(add3ifgreaterthan4_2_out_8));
  add3IfGreaterThan4 add3ifgreaterthan4_3 (
    .in_1(add3ifgreaterthan4_4_out_6), .in_2(add3ifgreaterthan4_4_out_7), .in_3(add3ifgreaterthan4_4_out_8),
    .in_4(add3ifgreaterthan4_16_out_5), .out_5(out_21), .out_6(out_22), .out_7(out_23), .out_8(out_24));
  add3IfGreaterThan4 add3ifgreaterthan4_4 (
    .in_1(add3ifgreaterthan4_5_out_6), .in_2(add3ifgreaterthan4_5_out_7), .in_3(add3ifgreaterthan4_5_out_8),
    .in_4(add3ifgreaterthan4_17_out_5), .out_5(out_20), .out_6(add3ifgreaterthan4_4_out_6),
    .out_7(add3ifgreaterthan4_4_out_7), .out_8(add3ifgreaterthan4_4_out_8));
  add3IfGreaterThan4 add3ifgreaterthan4_5 (
    .in_1(add3ifgreaterthan4_1_out_6), .in_2(add3ifgreaterthan4_1_out_7), .in_3(add3ifgreaterthan4_1_out_8),
    .in_4(add3ifgreaterthan4_6_out_5), .out_5(out_19), .out_6(add3ifgreaterthan4_5_out_6),
    .out_7(add3ifgreaterthan4_5_out_7), .out_8(add3ifgreaterthan4_5_out_8));
  add3IfGreaterThan4 add3ifgreaterthan4_6 (
    .in_1(add3ifgreaterthan4_7_out_6), .in_2(add3ifgreaterthan4_7_out_7), .in_3(add3ifgreaterthan4_7_out_8),
    .in_4(add3ifgreaterthan4_19_out_5), .out_5(add3ifgreaterthan4_6_out_5),
    .out_6(add3ifgreaterthan4_6_out_6), .out_7(add3ifgreaterthan4_6_out_7), .out_8(add3ifgreaterthan4_6_out_8));
  add3IfGreaterThan4 add3ifgreaterthan4_7 (
    .in_1(add3ifgreaterthan4_8_out_6), .in_2(add3ifgreaterthan4_8_out_7), .in_3(add3ifgreaterthan4_8_out_8),
    .in_4(add3ifgreaterthan4_20_out_5), .out_5(add3ifgreaterthan4_7_out_5),
    .out_6(add3ifgreaterthan4_7_out_6), .out_7(add3ifgreaterthan4_7_out_7), .out_8(add3ifgreaterthan4_7_out_8));
  add3IfGreaterThan4 add3ifgreaterthan4_8 (
    .in_1(add3ifgreaterthan4_9_out_6), .in_2(add3ifgreaterthan4_9_out_7), .in_3(add3ifgreaterthan4_9_out_8),
    .in_4(add3ifgreaterthan4_21_out_5), .out_5(add3ifgreaterthan4_8_out_5),
    .out_6(add3ifgreaterthan4_8_out_6), .out_7(add3ifgreaterthan4_8_out_7), .out_8(add3ifgreaterthan4_8_out_8));
  add3IfGreaterThan4 add3ifgreaterthan4_9 (
    .in_1(1'b0), .in_2(add3ifgreaterthan4_12_out_5), .in_3(add3ifgreaterthan4_11_out_5),
    .in_4(add3ifgreaterthan4_10_out_5), .out_5(add3ifgreaterthan4_9_out_5),
    .out_6(add3ifgreaterthan4_9_out_6), .out_7(add3ifgreaterthan4_9_out_7), .out_8(add3ifgreaterthan4_9_out_8));
  add3IfGreaterThan4 add3ifgreaterthan4_10 (
    .in_1(add3ifgreaterthan4_11_out_6), .in_2(add3ifgreaterthan4_11_out_7),
    .in_3(add3ifgreaterthan4_11_out_8), .in_4(add3ifgreaterthan4_23_out_5),
    .out_5(add3ifgreaterthan4_10_out_5), .out_6(add3ifgreaterthan4_10_out_6),
    .out_7(add3ifgreaterthan4_10_out_7), .out_8(add3ifgreaterthan4_10_out_8));
  add3IfGreaterThan4 add3ifgreaterthan4_11 (
    .in_1(add3ifgreaterthan4_12_out_6), .in_2(add3ifgreaterthan4_12_out_7),
    .in_3(add3ifgreaterthan4_12_out_8), .in_4(add3ifgreaterthan4_24_out_5),
    .out_5(add3ifgreaterthan4_11_out_5), .out_6(add3ifgreaterthan4_11_out_6),
    .out_7(add3ifgreaterthan4_11_out_7), .out_8(add3ifgreaterthan4_11_out_8));
  add3IfGreaterThan4 add3ifgreaterthan4_12 (
    .in_1(1'b0), .in_2(add3ifgreaterthan4_14_out_5), .in_3(add3ifgreaterthan4_13_out_5),
    .in_4(add3ifgreaterthan4_25_out_5), .out_5(add3ifgreaterthan4_12_out_5),
    .out_6(add3ifgreaterthan4_12_out_6), .out_7(add3ifgreaterthan4_12_out_7),
    .out_8(add3ifgreaterthan4_12_out_8));
  add3IfGreaterThan4 add3ifgreaterthan4_13 (
    .in_1(add3ifgreaterthan4_14_out_6), .in_2(add3ifgreaterthan4_14_out_7),
    .in_3(add3ifgreaterthan4_14_out_8), .in_4(in_4), .out_5(add3ifgreaterthan4_13_out_5),
    .out_6(add3ifgreaterthan4_13_out_6), .out_7(add3ifgreaterthan4_13_out_7),
    .out_8(add3ifgreaterthan4_13_out_8));
  add3IfGreaterThan4 add3ifgreaterthan4_14 (
    .in_1(1'b0), .in_2(in_1), .in_3(in_2), .in_4(in_3), .out_5(add3ifgreaterthan4_14_out_5),
    .out_6(add3ifgreaterthan4_14_out_6), .out_7(add3ifgreaterthan4_14_out_7),
    .out_8(add3ifgreaterthan4_14_out_8));
  add3IfGreaterThan4 add3ifgreaterthan4_15 (
    .in_1(add3ifgreaterthan4_16_out_6), .in_2(add3ifgreaterthan4_16_out_7),
    .in_3(add3ifgreaterthan4_16_out_8), .in_4(add3ifgreaterthan4_27_out_5), .out_5(out_25), .out_6(out_26),
    .out_7(out_27), .out_8(out_28));
  add3IfGreaterThan4 add3ifgreaterthan4_16 (
    .in_1(add3ifgreaterthan4_17_out_6), .in_2(add3ifgreaterthan4_17_out_7),
    .in_3(add3ifgreaterthan4_17_out_8), .in_4(add3ifgreaterthan4_28_out_5),
    .out_5(add3ifgreaterthan4_16_out_5), .out_6(add3ifgreaterthan4_16_out_6),
    .out_7(add3ifgreaterthan4_16_out_7), .out_8(add3ifgreaterthan4_16_out_8));
  add3IfGreaterThan4 add3ifgreaterthan4_17 (
    .in_1(add3ifgreaterthan4_6_out_6), .in_2(add3ifgreaterthan4_6_out_7), .in_3(add3ifgreaterthan4_6_out_8),
    .in_4(add3ifgreaterthan4_18_out_5), .out_5(add3ifgreaterthan4_17_out_5),
    .out_6(add3ifgreaterthan4_17_out_6), .out_7(add3ifgreaterthan4_17_out_7),
    .out_8(add3ifgreaterthan4_17_out_8));
  add3IfGreaterThan4 add3ifgreaterthan4_18 (
    .in_1(add3ifgreaterthan4_19_out_6), .in_2(add3ifgreaterthan4_19_out_7),
    .in_3(add3ifgreaterthan4_19_out_8), .in_4(add3ifgreaterthan4_30_out_5),
    .out_5(add3ifgreaterthan4_18_out_5), .out_6(add3ifgreaterthan4_18_out_6),
    .out_7(add3ifgreaterthan4_18_out_7), .out_8(add3ifgreaterthan4_18_out_8));
  add3IfGreaterThan4 add3ifgreaterthan4_19 (
    .in_1(add3ifgreaterthan4_20_out_6), .in_2(add3ifgreaterthan4_20_out_7),
    .in_3(add3ifgreaterthan4_20_out_8), .in_4(add3ifgreaterthan4_31_out_5),
    .out_5(add3ifgreaterthan4_19_out_5), .out_6(add3ifgreaterthan4_19_out_6),
    .out_7(add3ifgreaterthan4_19_out_7), .out_8(add3ifgreaterthan4_19_out_8));
  add3IfGreaterThan4 add3ifgreaterthan4_20 (
    .in_1(add3ifgreaterthan4_21_out_6), .in_2(add3ifgreaterthan4_21_out_7),
    .in_3(add3ifgreaterthan4_21_out_8), .in_4(add3ifgreaterthan4_32_out_5),
    .out_5(add3ifgreaterthan4_20_out_5), .out_6(add3ifgreaterthan4_20_out_6),
    .out_7(add3ifgreaterthan4_20_out_7), .out_8(add3ifgreaterthan4_20_out_8));
  add3IfGreaterThan4 add3ifgreaterthan4_21 (
    .in_1(add3ifgreaterthan4_10_out_6), .in_2(add3ifgreaterthan4_10_out_7),
    .in_3(add3ifgreaterthan4_10_out_8), .in_4(add3ifgreaterthan4_22_out_5),
    .out_5(add3ifgreaterthan4_21_out_5), .out_6(add3ifgreaterthan4_21_out_6),
    .out_7(add3ifgreaterthan4_21_out_7), .out_8(add3ifgreaterthan4_21_out_8));
  add3IfGreaterThan4 add3ifgreaterthan4_22 (
    .in_1(add3ifgreaterthan4_23_out_6), .in_2(add3ifgreaterthan4_23_out_7),
    .in_3(add3ifgreaterthan4_23_out_8), .in_4(in_8), .out_5(add3ifgreaterthan4_22_out_5),
    .out_6(add3ifgreaterthan4_22_out_6), .out_7(add3ifgreaterthan4_22_out_7),
    .out_8(add3ifgreaterthan4_22_out_8));
  add3IfGreaterThan4 add3ifgreaterthan4_23 (
    .in_1(add3ifgreaterthan4_24_out_6), .in_2(add3ifgreaterthan4_24_out_7),
    .in_3(add3ifgreaterthan4_24_out_8), .in_4(in_7), .out_5(add3ifgreaterthan4_23_out_5),
    .out_6(add3ifgreaterthan4_23_out_6), .out_7(add3ifgreaterthan4_23_out_7),
    .out_8(add3ifgreaterthan4_23_out_8));
  add3IfGreaterThan4 add3ifgreaterthan4_24 (
    .in_1(add3ifgreaterthan4_25_out_6), .in_2(add3ifgreaterthan4_25_out_7),
    .in_3(add3ifgreaterthan4_25_out_8), .in_4(in_6), .out_5(add3ifgreaterthan4_24_out_5),
    .out_6(add3ifgreaterthan4_24_out_6), .out_7(add3ifgreaterthan4_24_out_7),
    .out_8(add3ifgreaterthan4_24_out_8));
  add3IfGreaterThan4 add3ifgreaterthan4_25 (
    .in_1(add3ifgreaterthan4_13_out_6), .in_2(add3ifgreaterthan4_13_out_7),
    .in_3(add3ifgreaterthan4_13_out_8), .in_4(in_5), .out_5(add3ifgreaterthan4_25_out_5),
    .out_6(add3ifgreaterthan4_25_out_6), .out_7(add3ifgreaterthan4_25_out_7),
    .out_8(add3ifgreaterthan4_25_out_8));
  add3IfGreaterThan4 add3ifgreaterthan4_26 (
    .in_1(add3ifgreaterthan4_27_out_6), .in_2(add3ifgreaterthan4_27_out_7),
    .in_3(add3ifgreaterthan4_27_out_8), .in_4(add3ifgreaterthan4_34_out_5), .out_5(out_29), .out_6(out_30),
    .out_7(out_31), .out_8(out_32));
  add3IfGreaterThan4 add3ifgreaterthan4_27 (
    .in_1(add3ifgreaterthan4_28_out_6), .in_2(add3ifgreaterthan4_28_out_7),
    .in_3(add3ifgreaterthan4_28_out_8), .in_4(add3ifgreaterthan4_35_out_5),
    .out_5(add3ifgreaterthan4_27_out_5), .out_6(add3ifgreaterthan4_27_out_6),
    .out_7(add3ifgreaterthan4_27_out_7), .out_8(add3ifgreaterthan4_27_out_8));
  add3IfGreaterThan4 add3ifgreaterthan4_28 (
    .in_1(add3ifgreaterthan4_18_out_6), .in_2(add3ifgreaterthan4_18_out_7),
    .in_3(add3ifgreaterthan4_18_out_8), .in_4(add3ifgreaterthan4_29_out_5),
    .out_5(add3ifgreaterthan4_28_out_5), .out_6(add3ifgreaterthan4_28_out_6),
    .out_7(add3ifgreaterthan4_28_out_7), .out_8(add3ifgreaterthan4_28_out_8));
  add3IfGreaterThan4 add3ifgreaterthan4_29 (
    .in_1(add3ifgreaterthan4_30_out_6), .in_2(add3ifgreaterthan4_30_out_7),
    .in_3(add3ifgreaterthan4_30_out_8), .in_4(in_12), .out_5(add3ifgreaterthan4_29_out_5),
    .out_6(add3ifgreaterthan4_29_out_6), .out_7(add3ifgreaterthan4_29_out_7),
    .out_8(add3ifgreaterthan4_29_out_8));
  add3IfGreaterThan4 add3ifgreaterthan4_30 (
    .in_1(add3ifgreaterthan4_31_out_6), .in_2(add3ifgreaterthan4_31_out_7),
    .in_3(add3ifgreaterthan4_31_out_8), .in_4(in_11), .out_5(add3ifgreaterthan4_30_out_5),
    .out_6(add3ifgreaterthan4_30_out_6), .out_7(add3ifgreaterthan4_30_out_7),
    .out_8(add3ifgreaterthan4_30_out_8));
  add3IfGreaterThan4 add3ifgreaterthan4_31 (
    .in_1(add3ifgreaterthan4_32_out_6), .in_2(add3ifgreaterthan4_32_out_7),
    .in_3(add3ifgreaterthan4_32_out_8), .in_4(in_10), .out_5(add3ifgreaterthan4_31_out_5),
    .out_6(add3ifgreaterthan4_31_out_6), .out_7(add3ifgreaterthan4_31_out_7),
    .out_8(add3ifgreaterthan4_31_out_8));
  add3IfGreaterThan4 add3ifgreaterthan4_32 (
    .in_1(add3ifgreaterthan4_22_out_6), .in_2(add3ifgreaterthan4_22_out_7),
    .in_3(add3ifgreaterthan4_22_out_8), .in_4(in_9), .out_5(add3ifgreaterthan4_32_out_5),
    .out_6(add3ifgreaterthan4_32_out_6), .out_7(add3ifgreaterthan4_32_out_7),
    .out_8(add3ifgreaterthan4_32_out_8));
  add3IfGreaterThan4 add3ifgreaterthan4_33 (
    .in_1(add3ifgreaterthan4_34_out_6), .in_2(add3ifgreaterthan4_34_out_7),
    .in_3(add3ifgreaterthan4_34_out_8), .in_4(in_15), .out_5(out_33), .out_6(out_34), .out_7(out_35),
    .out_8(out_36));
  add3IfGreaterThan4 add3ifgreaterthan4_34 (
    .in_1(add3ifgreaterthan4_35_out_6), .in_2(add3ifgreaterthan4_35_out_7),
    .in_3(add3ifgreaterthan4_35_out_8), .in_4(in_14), .out_5(add3ifgreaterthan4_34_out_5),
    .out_6(add3ifgreaterthan4_34_out_6), .out_7(add3ifgreaterthan4_34_out_7),
    .out_8(add3ifgreaterthan4_34_out_8));
  add3IfGreaterThan4 add3ifgreaterthan4_35 (
    .in_1(add3ifgreaterthan4_29_out_6), .in_2(add3ifgreaterthan4_29_out_7),
    .in_3(add3ifgreaterthan4_29_out_8), .in_4(in_13), .out_5(add3ifgreaterthan4_35_out_5),
    .out_6(add3ifgreaterthan4_35_out_6), .out_7(add3ifgreaterthan4_35_out_7),
    .out_8(add3ifgreaterthan4_35_out_8));

  assign out_37 = in_16;
endmodule

module bcdTo7seg (
);

  binToBcd bintobcd_1 ();  // open: out_17, out_18, out_19, out_20, out_21, out_22, out_23, out_24, out_25, out_26, out_27, out_28, out_29, out_30, out_31, out_32, out_33, out_34, out_35, out_36, out_37, in_1, in_2, in_3, in_4, in_5, in_6, in_7, in_8, in_9, in_10, in_11, in_12, in_13, in_14, in_15, in_16
endmodule

module _7segHex (
  input  A,
  input  B,
  input  C,
  input  D,
  output out_5,
  output out_6,
  output out_7,
  output out_8,
  output out_9,
  output out_10,
  output out_11
);

  wire and_1_out, and_2_out, and_3_out, and_4_out, and_5_out, and_6_out, and_7_out, and_8_out, and_9_out,
       and_10_out, and_11_out, and_12_out, and_13_out, and_14_out, and_15_out, and_16_out, and_17_out,
       and_18_out, and_19_out, and_20_out, and_21_out, and_22_out, and_23_out, and_24_out, and_25_out,
       and_26_out, and_27_out, and_28_out, and_29_out, and_30_out, and_31_out, and_32_out, and_33_out,
       and_34_out, and_35_out, not_1_out, not_2_out, not_3_out, not_4_out;

  not not_1 (not_1_out, A);
  not not_2 (not_2_out, B);
  not not_3 (not_3_out, C);
  not not_4 (not_4_out, D);
  and and_1 (and_1_out, not_2_out, not_4_out);
  and and_2 (and_2_out, not_1_out, not_2_out);
  and and_3 (and_3_out, A, not_3_out, D);
  and and_4 (and_4_out, not_1_out, C, D);
  and and_5 (and_5_out, not_4_out, not_3_out, not_1_out);
  and and_6 (and_6_out, A, not_2_out);
  and and_7 (and_7_out, not_1_out, B);
  and and_8 (and_8_out, not_3_out, D);
  and and_9 (and_9_out, not_1_out, not_3_out);
  and and_10 (and_10_out, not_1_out, D);
  and and_11 (and_11_out, A, not_3_out);
  and and_12 (and_12_out, B, not_3_out, D);
  and and_13 (and_13_out, not_2_out, C, D);
  and and_14 (and_14_out, not_4_out, not_2_out, not_1_out);
  and and_15 (and_15_out, not_4_out, C, B);
  and and_16 (and_16_out, C, not_4_out);
  and and_17 (and_17_out, A, B);
  and and_18 (and_18_out, A, C);
  and and_19 (and_19_out, not_2_out, not_4_out);
  and and_20 (and_20_out, A, not_2_out);
  and and_21 (and_21_out, not_3_out, not_4_out);
  and and_22 (and_22_out, A, C);
  and and_23 (and_23_out, not_1_out, B, not_3_out);
  and and_24 (and_24_out, B, C, not_4_out);
  and and_25 (and_25_out, not_4_out, not_2_out);
  and and_26 (and_26_out, not_1_out, C);
  and and_27 (and_27_out, A, not_4_out);
  and and_28 (and_28_out, C, B);
  and and_29 (and_29_out, not_1_out, D, B);
  and and_30 (and_30_out, A, not_2_out, not_3_out);
  and and_31 (and_31_out, C, not_4_out);
  and and_32 (and_32_out, A, D);
  and and_33 (and_33_out, A, not_2_out);
  and and_34 (and_34_out, not_2_out, not_1_out, C);
  and and_35 (and_35_out, not_3_out, B, not_1_out);
  or or_1 (out_9, and_20_out, and_21_out, and_22_out, and_23_out, and_24_out);
  or or_2 (out_5, and_1_out, and_2_out, and_3_out, and_4_out, and_5_out);
  or or_3 (out_6, and_6_out, and_7_out, and_8_out, and_9_out, and_10_out);
  or or_4 (out_7, and_11_out, and_12_out, and_13_out, and_14_out, and_15_out);
  or or_5 (out_8, and_16_out, and_17_out, and_18_out, and_19_out);
  or or_6 (out_10, and_25_out, and_26_out, and_27_out, and_28_out, and_29_out, and_30_out);
  or or_7 (out_11, and_31_out, and_32_out, and_33_out, and_34_out, and_35_out);
endmodule

module Calculator (
  input  in_1,
  input  in_2,
  input  in_3,
  input  in_4,
  input  in_5,
  input  in_6,
  input  in_7,
  input  in_8,
  input  in_9,
  input  in_10,
  input  in_11,
  input  in_12,
  input  in_13,
  input  in_14,
  input  in_15,
  input  in_16,
  input  in_17,
  input  in_18,
  input  [1:0] in_19
);

  wire A0, A1, A2, A3, and_1_out, B0, B1, B2, B3, bintobcd_1_out_22, bintobcd_1_out_23, bintobcd_1_out_24,
       bintobcd_1_out_25, bintobcd_1_out_26, bintobcd_1_out_27, bintobcd_1_out_28, bintobcd_1_out_29,
       bintobcd_1_out_30, bintobcd_1_out_31, bintobcd_1_out_32, bintobcd_1_out_33, bintobcd_1_out_34,
       bintobcd_1_out_35, bintobcd_1_out_36, bintobcd_1_out_37, C0, C1, C2, C3, D0, D1, D2, D3, E0, E1, E2,
       E3, lookaheadaddersubtractor_1_s0, lookaheadaddersubtractor_1_s1, lookaheadaddersubtractor_1_s2,
       lookaheadaddersubtractor_1_s3, lookaheadaddersubtractor_1_s4, lookaheadaddersubtractor_1_s5,
       lookaheadaddersubtractor_1_s6, lookaheadaddersubtractor_1_s7, n7seghex_1_out_5, n7seghex_1_out_6,
       n7seghex_1_out_7, n7seghex_1_out_8, n7seghex_1_out_9, n7seghex_1_out_10, n7seghex_1_out_11,
       n7seghex_2_out_5, n7seghex_2_out_6, n7seghex_2_out_7, n7seghex_2_out_8, n7seghex_2_out_9,
       n7seghex_2_out_10, n7seghex_2_out_11, n7seghex_3_out_5, n7seghex_3_out_6, n7seghex_3_out_7,
       n7seghex_3_out_8, n7seghex_3_out_9, n7seghex_3_out_10, n7seghex_3_out_11, n7seghex_4_out_5,
       n7seghex_4_out_6, n7seghex_4_out_7, n7seghex_4_out_8, n7seghex_4_out_9, n7seghex_4_out_10,
       n7seghex_4_out_11, n7seghex_5_out_5, n7seghex_5_out_6, n7seghex_5_out_7, n7seghex_5_out_8,
       n7seghex_5_out_9, n7seghex_5_out_10, n7seghex_5_out_11, not_1_out, not_2_out, Overflow, Sign;
  wire [7:0] Quotient, Remainder, Sum;
  wire [15:0] Multiplication, Output;

  divider divider_1 (
    .in_1(in_9), .in_2(in_10), .in_3(in_11), .in_4(in_12), .in_5(in_13), .in_6(in_14), .in_7(in_15),
    .in_8(in_16), .in_9(in_1), .in_10(in_2), .in_11(in_3), .in_12(in_4), .in_13(in_5), .in_14(in_6),
    .in_15(in_7), .in_16(in_8), .out_17(Quotient[7]), .out_25(Remainder[7]), .out_18(Quotient[6]),
    .out_26(Remainder[6]), .out_19(Quotient[5]), .out_27(Remainder[5]), .out_20(Quotient[4]),
    .out_28(Remainder[4]), .out_21(Quotient[3]), .out_29(Remainder[3]), .out_22(Quotient[2]),
    .out_30(Remainder[2]), .out_23(Quotient[1]), .out_31(Remainder[1]), .out_24(Quotient[0]),
    .out_32(Remainder[0]));
  Multiplier multiplier_1 (
    .out_17(Multiplication[0]), .out_18(Multiplication[1]), .out_19(Multiplication[2]),
    .out_20(Multiplication[3]), .out_21(Multiplication[4]), .out_22(Multiplication[5]),
    .out_23(Multiplication[6]), .out_24(Multiplication[7]), .out_25(Multiplication[8]),
    .out_26(Multiplication[9]), .out_27(Multiplication[10]), .out_28(Multiplication[11]),
    .out_29(Multiplication[12]), .out_30(Multiplication[13]), .out_31(Multiplication[14]), .in_1(in_1),
    .in_2(in_2), .in_3(in_3), .in_4(in_4), .in_5(in_5), .in_6(in_6), .in_7(in_7), .in_8(in_8), .in_9(in_9),
    .in_10(in_10), .in_11(in_11), .in_12(in_12), .in_13(in_13), .in_14(in_14), .in_15(in_15), .in_16(in_16),
    .out_32(Multiplication[15]));
  lookaheadAdderSubtractor lookaheadaddersubtractor_1 (
    .M(in_18), .S0(lookaheadaddersubtractor_1_s0), .S1(lookaheadaddersubtractor_1_s1),
    .S2(lookaheadaddersubtractor_1_s2), .S3(lookaheadaddersubtractor_1_s3),
    .S4(lookaheadaddersubtractor_1_s4), .S5(lookaheadaddersubtractor_1_s5),
    .S6(lookaheadaddersubtractor_1_s6), .S7(lookaheadaddersubtractor_1_s7), .in_16(in_1), .A7(in_2),
    .A6(in_3), .A5(in_4), .A4(in_5), .A3(in_6), .A2(in_7), .A1(in_8), .B7(in_9), .B6(in_10), .B5(in_11),
    .B4(in_12), .B3(in_13), .B2(in_14), .B1(in_15), .B0(in_16), .V(Overflow), .Sign(Sign));
  lookaheadAdderSubtractor lookaheadaddersubtractor_2 (
    .M(lookaheadaddersubtractor_1_s7), .S0(Sum[0]), .S1(Sum[1]), .S2(Sum[2]), .S3(Sum[3]), .S4(Sum[4]),
    .S5(Sum[5]), .S6(Sum[6]), .S7(Sum[7]), .in_16(1'b0), .A7(1'b0), .A6(1'b0), .A5(1'b0), .A4(1'b0),
    .A3(1'b0), .A2(1'b0), .A1(1'b0), .B7(lookaheadaddersubtractor_1_s7), .B6(lookaheadaddersubtractor_1_s6),
    .B5(lookaheadaddersubtractor_1_s5), .B4(lookaheadaddersubtractor_1_s4),
    .B3(lookaheadaddersubtractor_1_s3), .B2(lookaheadaddersubtractor_1_s2),
    .B1(lookaheadaddersubtractor_1_s1), .B0(lookaheadaddersubtractor_1_s0));  // open: V, Sign
  and and_1 (and_1_out, lookaheadaddersubtractor_1_s7, not_1_out, not_2_out);
  not not_1 (not_1_out, in_19[1]);
  binToBcd bintobcd_1 (
    .out_18(E3), .out_19(E2), .out_20(E1), .out_21(E0), .out_22(bintobcd_1_out_22),
    .out_23(bintobcd_1_out_23), .out_24(bintobcd_1_out_24), .out_25(bintobcd_1_out_25),
    .out_26(bintobcd_1_out_26), .out_27(bintobcd_1_out_27), .out_28(bintobcd_1_out_28),
    .out_29(bintobcd_1_out_29), .out_30(bintobcd_1_out_30), .out_31(bintobcd_1_out_31),
    .out_32(bintobcd_1_out_32), .out_33(bintobcd_1_out_33), .out_34(bintobcd_1_out_34),
    .out_35(bintobcd_1_out_35), .out_36(bintobcd_1_out_36), .out_37(bintobcd_1_out_37), .in_1(Output[15]),
    .in_2(Output[14]), .in_3(Output[13]), .in_4(Output[12]), .in_5(Output[11]), .in_6(Output[10]),
    .in_7(Output[9]), .in_8(Output[8]), .in_9(Output[7]), .in_10(Output[6]), .in_11(Output[5]),
    .in_12(Output[4]), .in_13(Output[3]), .in_14(Output[2]), .in_15(Output[1]), .in_16(Output[0]));  // open: out_17
  not not_2 (not_2_out, in_19[0]);
  Multiplexer #(.select(2), .width(16), .enable("false")) multiplexer_1 (
    .in0({{8{1'b0}}, Sum}), .in1(Multiplication), .in2({{8{1'b0}}, Quotient}), .in3({{8{1'b0}}, Remainder}),
    .out(Output), .sel(in_19));
  LED led_1 (.in(Overflow));
  _7_Segment_Display u_7_segment_display_1 (.g(and_1_out));  // open: f, a, b, e, d, c, dp
  _7_Segment_Display u_7_segment_display_2 (
    .g(n7seghex_1_out_11), .f(n7seghex_1_out_9), .a(n7seghex_1_out_10), .b(n7seghex_1_out_5),
    .e(n7seghex_1_out_8), .d(n7seghex_1_out_7), .c(n7seghex_1_out_6));  // open: dp
  _7segHex u_7seghex_1 (
    .out_5(n7seghex_1_out_5), .out_6(n7seghex_1_out_6), .out_7(n7seghex_1_out_7), .out_8(n7seghex_1_out_8),
    .out_9(n7seghex_1_out_9), .out_10(n7seghex_1_out_10), .out_11(n7seghex_1_out_11), .A(E3), .B(E2), .C(E1),
    .D(E0));
  _7_Segment_Display u_7_segment_display_3 (
    .g(n7seghex_2_out_11), .f(n7seghex_2_out_9), .a(n7seghex_2_out_10), .b(n7seghex_2_out_5),
    .e(n7seghex_2_out_8), .d(n7seghex_2_out_7), .c(n7seghex_2_out_6));  // open: dp
  _7segHex u_7seghex_2 (
    .out_5(n7seghex_2_out_5), .out_6(n7seghex_2_out_6), .out_7(n7seghex_2_out_7), .out_8(n7seghex_2_out_8),
    .out_9(n7seghex_2_out_9), .out_10(n7seghex_2_out_10), .out_11(n7seghex_2_out_11), .A(D3), .B(D2), .C(D1),
    .D(D0));
  _16bitSelect u_16bitselect_1 (
    .in_1(in_17), .out_34(D3), .out_35(D2), .out_36(D1), .out_37(D0), .out_38(C3), .out_39(C2), .out_40(C1),
    .out_41(C0), .out_42(B3), .out_43(B2), .out_44(B1), .out_45(B0), .out_46(A3), .out_47(A2), .out_48(A1),
    .out_49(A0), .in_2(Output[15]), .in_3(bintobcd_1_out_22), .in_4(Output[14]), .in_5(bintobcd_1_out_23),
    .in_6(Output[13]), .in_7(bintobcd_1_out_24), .in_8(Output[12]), .in_9(bintobcd_1_out_25),
    .in_10(Output[11]), .in_11(bintobcd_1_out_26), .in_12(Output[10]), .in_13(bintobcd_1_out_27),
    .in_14(Output[9]), .in_15(bintobcd_1_out_28), .in_16(Output[8]), .in_17(bintobcd_1_out_29),
    .in_18(Output[7]), .in_19(bintobcd_1_out_30), .in_20(Output[6]), .in_21(bintobcd_1_out_31),
    .in_22(Output[5]), .in_23(bintobcd_1_out_32), .in_24(Output[4]), .in_25(bintobcd_1_out_33),
    .in_26(Output[3]), .in_27(bintobcd_1_out_34), .in_28(Output[2]), .in_29(bintobcd_1_out_35),
    .in_30(Output[1]), .in_31(bintobcd_1_out_36), .in_32(Output[0]), .in_33(bintobcd_1_out_37));
  _7_Segment_Display u_7_segment_display_4 (
    .g(n7seghex_3_out_11), .f(n7seghex_3_out_9), .a(n7seghex_3_out_10), .b(n7seghex_3_out_5),
    .e(n7seghex_3_out_8), .d(n7seghex_3_out_7), .c(n7seghex_3_out_6));  // open: dp
  _7segHex u_7seghex_3 (
    .out_5(n7seghex_3_out_5), .out_6(n7seghex_3_out_6), .out_7(n7seghex_3_out_7), .out_8(n7seghex_3_out_8),
    .out_9(n7seghex_3_out_9), .out_10(n7seghex_3_out_10), .out_11(n7seghex_3_out_11), .A(C3), .B(C2), .C(C1),
    .D(C0));
  _7_Segment_Display u_7_segment_display_5 (
    .g(n7seghex_4_out_11), .f(n7seghex_4_out_9), .a(n7seghex_4_out_10), .b(n7seghex_4_out_5),
    .e(n7seghex_4_out_8), .d(n7seghex_4_out_7), .c(n7seghex_4_out_6));  // open: dp
  _7segHex u_7seghex_4 (
    .out_5(n7seghex_4_out_5), .out_6(n7seghex_4_out_6), .out_7(n7seghex_4_out_7), .out_8(n7seghex_4_out_8),
    .out_9(n7seghex_4_out_9), .out_10(n7seghex_4_out_10), .out_11(n7seghex_4_out_11), .A(B3), .B(B2), .C(B1),
    .D(B0));
  _7_Segment_Display u_7_segment_display_6 (
    .g(n7seghex_5_out_11), .f(n7seghex_5_out_9), .a(n7seghex_5_out_10), .b(n7seghex_5_out_5),
    .e(n7seghex_5_out_8), .d(n7seghex_5_out_7), .c(n7seghex_5_out_6));  // open: dp
  _7segHex u_7seghex_5 (
    .out_5(n7seghex_5_out_5), .out_6(n7seghex_5_out_6), .out_7(n7seghex_5_out_7), .out_8(n7seghex_5_out_8),
    .out_9(n7seghex_5_out_9), .out_10(n7seghex_5_out_10), .out_11(n7seghex_5_out_11), .A(A3), .B(A2), .C(A1),
    .D(A0));

  // Other names for the same wires on the sheet: Hex_Decimal = in_17; InA0 = in_8; InA1 = in_7; InA2 = in_6;
  //   InA3 = in_5; InA4 = in_4; InA5 = in_3; InA6 = in_2; InA7 = in_1; InB0 = in_16; InB1 = in_15; InB2 = in_14;
  //   InB3 = in_13; InB4 = in_12; InB5 = in_11; InB6 = in_10; InB7 = in_9
endmodule

module _16bitSelect (
  input  in_1,
  input  in_2,
  input  in_3,
  input  in_4,
  input  in_5,
  input  in_6,
  input  in_7,
  input  in_8,
  input  in_9,
  input  in_10,
  input  in_11,
  input  in_12,
  input  in_13,
  input  in_14,
  input  in_15,
  input  in_16,
  input  in_17,
  input  in_18,
  input  in_19,
  input  in_20,
  input  in_21,
  input  in_22,
  input  in_23,
  input  in_24,
  input  in_25,
  input  in_26,
  input  in_27,
  input  in_28,
  input  in_29,
  input  in_30,
  input  in_31,
  input  in_32,
  input  in_33,
  output out_34,
  output out_35,
  output out_36,
  output out_37,
  output out_38,
  output out_39,
  output out_40,
  output out_41,
  output out_42,
  output out_43,
  output out_44,
  output out_45,
  output out_46,
  output out_47,
  output out_48,
  output out_49
);

  Multiplexer multiplexer_1 (.in0(in_2), .in1(in_3), .out(out_34), .sel(in_1), .en(1'b1));
  Multiplexer multiplexer_2 (.in0(in_6), .in1(in_7), .out(out_36), .sel(in_1), .en(1'b1));
  Multiplexer multiplexer_3 (.in0(in_4), .in1(in_5), .out(out_35), .sel(in_1), .en(1'b1));
  Multiplexer multiplexer_4 (.in0(in_8), .in1(in_9), .out(out_37), .sel(in_1), .en(1'b1));
  Multiplexer multiplexer_5 (.in0(in_10), .in1(in_11), .out(out_38), .sel(in_1), .en(1'b1));
  Multiplexer multiplexer_6 (.in0(in_12), .in1(in_13), .out(out_39), .sel(in_1), .en(1'b1));
  Multiplexer multiplexer_7 (.in0(in_14), .in1(in_15), .out(out_40), .sel(in_1), .en(1'b1));
  Multiplexer multiplexer_8 (.in0(in_16), .in1(in_17), .out(out_41), .sel(in_1), .en(1'b1));
  Multiplexer multiplexer_9 (.in0(in_18), .in1(in_19), .out(out_42), .sel(in_1), .en(1'b1));
  Multiplexer multiplexer_10 (.in0(in_20), .in1(in_21), .out(out_43), .sel(in_1), .en(1'b1));
  Multiplexer multiplexer_11 (.in0(in_22), .in1(in_23), .out(out_44), .sel(in_1), .en(1'b1));
  Multiplexer multiplexer_12 (.in0(in_24), .in1(in_25), .out(out_45), .sel(in_1), .en(1'b1));
  Multiplexer multiplexer_13 (.in0(in_28), .in1(in_29), .out(out_47), .sel(in_1), .en(1'b1));
  Multiplexer multiplexer_14 (.in0(in_26), .in1(in_27), .out(out_46), .sel(in_1), .en(1'b1));
  Multiplexer multiplexer_15 (.in0(in_32), .in1(in_33), .out(out_49), .sel(in_1), .en(1'b1));
  Multiplexer multiplexer_16 (.in0(in_30), .in1(in_31), .out(out_48), .sel(in_1), .en(1'b1));
endmodule
