// Logisim project full-adder-and-twos-complement.circ as structural Verilog: 1 circuit, main circuit main
module main (
  input  in_1,
  input  in_2,
  input  in_3,
  input  in_4,
  input  in_5,
  input  in_6,
  input  in_7,
  input  in_8,
  input  in_9,
  input  in_10,
  input  in_11,
  input  in_12,
  input  in_13,
  input  in_14,
  input  in_15,
  input  in_16,
  input  in_17,
  input  in_18,
  input  in_19,
  input  in_20,
  input  in_21,
  input  in_22,
  input  in_23,
  input  in_24,
  input  in_25,
  input  in_26,
  input  in_27,
  input  in_28,
  input  in_29,
  input  in_30,
  input  in_31,
  input  in_32,
  input  in_33,
  input  in_34,
  input  in_35,
  input  in_36,
  input  in_37,
  input  in_38,
  input  in_39,
  input  in_40,
  input  in_41,
  input  in_42,
  input  in_43,
  input  in_44,
  input  in_45,
  input  in_46,
  input  in_47,
  input  in_48,
  input  in_49,
  input  in_50,
  input  in_51,
  input  in_52,
  input  in_53,
  input  in_54,
  input  in_55,
  input  in_56,
  input  in_57,
  input  in_58,
  input  in_59
);

  wire and_1_out, and_2_out, and_3_out, and_4_out, and_5_out, and_6_out, and_7_out, and_8_out, and_9_out,
       and_10_out, and_11_out, and_12_out, and_13_out, and_14_out, and_15_out, and_16_out, and_17_out,
       and_18_out, and_19_out, and_20_out, and_21_out, and_22_out, and_23_out, and_24_out, and_25_out,
       and_26_out, and_27_out, and_28_out, and_29_out, and_30_out, and_31_out, and_32_out, and_33_out,
       and_34_out, and_35_out, and_36_out, and_37_out, and_38_out, and_39_out, and_40_out, and_41_out,
       and_42_out, and_43_out, and_44_out, and_45_out, and_46_out, and_47_out, and_48_out, and_49_out,
       and_50_out, and_51_out, and_52_out, and_53_out, and_54_out, and_55_out, and_56_out, and_57_out,
       and_58_out, and_59_out, and_60_out, and_61_out, and_62_out, and_63_out, and_64_out, and_65_out,
       and_66_out, and_67_out, and_68_out, and_69_out, and_70_out, and_71_out, and_72_out, not_1_out,
       not_2_out, not_3_out, not_4_out, not_5_out, not_6_out, not_7_out, not_8_out, or_1_out, or_2_out,
       or_3_out, or_4_out, or_5_out, or_6_out, or_7_out, or_8_out, or_9_out, or_10_out, or_11_out, or_12_out,
       or_13_out, or_14_out, or_15_out, or_16_out, or_17_out, or_18_out, or_19_out, or_20_out, or_21_out,
       or_22_out, or_23_out, or_24_out, undriven, undriven_2, undriven_3, undriven_4, undriven_5, undriven_6,
       undriven_7, undriven_8, undriven_9, undriven_10, undriven_11, undriven_12, undriven_13, undriven_14,
       undriven_15, undriven_16, undriven_17, undriven_18, undriven_19, undriven_20, undriven_21,
       undriven_22, undriven_23, undriven_24, undriven_25, undriven_26, undriven_27, undriven_28,
       undriven_29, undriven_30, xor_1_out, xor_2_out, xor_3_out, xor_4_out, xor_5_out, xor_6_out, xor_7_out,
       xor_8_out, xor_9_out, xor_10_out, xor_11_out, xor_12_out, xor_13_out, xor_14_out, xor_15_out,
       xor_16_out, xor_17_out, xor_18_out, xor_19_out, xor_20_out, xor_21_out, xor_22_out, xor_23_out,
       xor_24_out, xor_25_out, xor_26_out, xor_27_out, xor_28_out, xor_29_out, xor_30_out, xor_31_out,
       xor_32_out, xor_33_out, xor_34_out, xor_35_out, xor_36_out, xor_37_out, xor_38_out, xor_39_out,
       xor_40_out, xor_41_out, xor_42_out, xor_43_out, xor_44_out, xor_45_out, xor_46_out, xor_47_out,
       xor_48_out, xor_49_out, xor_50_out, xor_51_out, xor_52_out, xor_53_out, xor_54_out, xor_55_out,
       xor_56_out;

  or or_1 (or_1_out, and_1_out, and_2_out);
  and and_1 (and_1_out, in_1, in_2);
  and and_2 (and_2_out, xor_1_out, or_3_out);
  and and_3 (and_3_out, not_1_out, and_8_out);
  and and_4 (and_4_out, undriven, undriven_2);
  or or_2 (or_2_out, and_4_out, and_5_out);
  and and_5 (and_5_out, xor_4_out, or_5_out);
  or or_3 (or_3_out, and_9_out, and_10_out);
  xor xor_1 (xor_1_out, in_1, in_2);
  xor xor_2 (xor_2_out, xor_1_out, or_3_out);
  and and_6 (and_6_out, in_34, undriven_3);
  or or_4 (or_4_out, and_6_out, and_7_out);
  and and_7 (and_7_out, xor_6_out, or_7_out);
  not not_1 (not_1_out, in_42);
  and and_8 (and_8_out, not_2_out, and_15_out);
  xor xor_3 (xor_3_out, not_1_out, and_8_out);
  xor xor_4 (xor_4_out, undriven, undriven_2);
  xor xor_5 (xor_5_out, xor_4_out, or_5_out);
  and and_9 (and_9_out, in_3, in_4);
  and and_10 (and_10_out, xor_9_out, or_6_out);
  xor xor_6 (xor_6_out, in_34, undriven_3);
  xor xor_7 (xor_7_out, xor_6_out, or_7_out);
  not not_2 (not_2_out, in_43);
  xor xor_8 (xor_8_out, not_2_out, and_15_out);
  and and_11 (and_11_out, undriven_4, undriven_5);
  or or_5 (or_5_out, and_11_out, and_12_out);
  and and_12 (and_12_out, xor_11_out, or_8_out);
  or or_6 (or_6_out, and_16_out, and_17_out);
  xor xor_9 (xor_9_out, in_3, in_4);
  xor xor_10 (xor_10_out, xor_9_out, or_6_out);
  and and_13 (and_13_out, in_36, undriven_6);
  or or_7 (or_7_out, and_13_out, and_14_out);
  and and_14 (and_14_out, xor_13_out, or_10_out);
  and and_15 (and_15_out, not_3_out, and_18_out);
  xor xor_11 (xor_11_out, undriven_4, undriven_5);
  xor xor_12 (xor_12_out, xor_11_out, or_8_out);
  and and_16 (and_16_out, in_5, in_6);
  and and_17 (and_17_out, xor_16_out, or_9_out);
  xor xor_13 (xor_13_out, in_36, undriven_6);
  xor xor_14 (xor_14_out, xor_13_out, or_10_out);
  not not_3 (not_3_out, in_44);
  and and_18 (and_18_out, not_4_out, and_23_out);
  xor xor_15 (xor_15_out, not_3_out, and_18_out);
  and and_19 (and_19_out, undriven_7, undriven_8);
  or or_8 (or_8_out, and_19_out, and_20_out);
  and and_20 (and_20_out, xor_19_out, or_11_out);
  or or_9 (or_9_out, and_24_out, and_25_out);
  xor xor_16 (xor_16_out, in_5, in_6);
  xor xor_17 (xor_17_out, xor_16_out, or_9_out);
  and and_21 (and_21_out, in_38, undriven_9);
  or or_10 (or_10_out, and_21_out, and_22_out);
  and and_22 (and_22_out, xor_21_out, or_13_out);
  not not_4 (not_4_out, in_45);
  and and_23 (and_23_out, not_5_out, and_26_out);
  xor xor_18 (xor_18_out, not_4_out, and_23_out);
  xor xor_19 (xor_19_out, undriven_7, undriven_8);
  xor xor_20 (xor_20_out, xor_19_out, or_11_out);
  and and_24 (and_24_out, in_7, in_8);
  and and_25 (and_25_out, xor_24_out, or_12_out);
  xor xor_21 (xor_21_out, in_38, undriven_9);
  xor xor_22 (xor_22_out, xor_21_out, or_13_out);
  not not_5 (not_5_out, in_46);
  and and_26 (and_26_out, not_6_out, and_33_out);
  xor xor_23 (xor_23_out, not_5_out, and_26_out);
  and and_27 (and_27_out, undriven_10, undriven_11);
  or or_11 (or_11_out, and_27_out, and_28_out);
  and and_28 (and_28_out, xor_27_out, or_14_out);
  or or_12 (or_12_out, and_31_out, and_32_out);
  xor xor_24 (xor_24_out, in_7, in_8);
  xor xor_25 (xor_25_out, xor_24_out, or_12_out);
  and and_29 (and_29_out, in_40, undriven_12);
  or or_13 (or_13_out, and_29_out, and_30_out);
  and and_30 (and_30_out, xor_29_out, undriven_13);
  not not_6 (not_6_out, in_47);
  xor xor_26 (xor_26_out, not_6_out, and_33_out);
  xor xor_27 (xor_27_out, undriven_10, undriven_11);
  xor xor_28 (xor_28_out, xor_27_out, or_14_out);
  and and_31 (and_31_out, in_9, in_10);
  and and_32 (and_32_out, xor_31_out, or_15_out);
  xor xor_29 (xor_29_out, in_40, undriven_12);
  xor xor_30 (xor_30_out, xor_29_out, undriven_13);
  and and_33 (and_33_out, not_7_out, and_36_out);
  and and_34 (and_34_out, undriven_14, undriven_15);
  or or_14 (or_14_out, and_34_out, and_35_out);
  and and_35 (and_35_out, xor_34_out, or_16_out);
  or or_15 (or_15_out, and_37_out, and_38_out);
  xor xor_31 (xor_31_out, in_9, in_10);
  xor xor_32 (xor_32_out, xor_31_out, or_15_out);
  not not_7 (not_7_out, in_48);
  and and_36 (and_36_out, not_8_out, in_50);
  xor xor_33 (xor_33_out, not_7_out, and_36_out);
  xor xor_34 (xor_34_out, undriven_14, undriven_15);
  xor xor_35 (xor_35_out, xor_34_out, or_16_out);
  and and_37 (and_37_out, in_11, in_12);
  and and_38 (and_38_out, xor_37_out, or_17_out);
  not not_8 (not_8_out, in_49);
  xor xor_36 (xor_36_out, not_8_out, in_50);
  and and_39 (and_39_out, undriven_16, undriven_17);
  or or_16 (or_16_out, and_39_out, and_40_out);
  and and_40 (and_40_out, xor_39_out, or_18_out);
  or or_17 (or_17_out, and_41_out, and_42_out);
  xor xor_37 (xor_37_out, in_11, in_12);
  xor xor_38 (xor_38_out, xor_37_out, or_17_out);
  xor xor_39 (xor_39_out, undriven_16, undriven_17);
  xor xor_40 (xor_40_out, xor_39_out, or_18_out);
  and and_41 (and_41_out, in_13, in_14);
  and and_42 (and_42_out, xor_41_out, or_19_out);
  and and_43 (and_43_out, undriven_18, undriven_19);
  or or_18 (or_18_out, and_43_out, and_44_out);
  and and_44 (and_44_out, xor_43_out, or_20_out);
  or or_19 (or_19_out, and_45_out, and_46_out);
  xor xor_41 (xor_41_out, in_13, in_14);
  xor xor_42 (xor_42_out, xor_41_out, or_19_out);
  xor xor_43 (xor_43_out, undriven_18, undriven_19);
  xor xor_44 (xor_44_out, xor_43_out, or_20_out);
  and and_45 (and_45_out, in_15, in_16);
  and and_46 (and_46_out, xor_45_out, in_17);
  and and_47 (and_47_out, undriven_20, undriven_21);
  or or_20 (or_20_out, and_47_out, and_48_out);
  and and_48 (and_48_out, xor_47_out, in_51);
  xor xor_45 (xor_45_out, in_15, in_16);
  xor xor_46 (xor_46_out, xor_45_out, in_17);
  xor xor_47 (xor_47_out, undriven_20, undriven_21);
  xor xor_48 (xor_48_out, xor_47_out, in_51);
  or or_21 (or_21_out, and_49_out, and_50_out);
  and and_49 (and_49_out, undriven_22, undriven_23);
  // XOR_Gate xor_49 has open pins: out=xor_49_out
  and and_50 (and_50_out, xor_49_out, or_22_out);
  or or_22 (or_22_out, and_51_out, and_52_out);
  // XOR_Gate xor_50 has open pins: out=xor_50_out
  and and_51 (and_51_out, undriven_24, undriven_25);
  // XOR_Gate xor_51 has open pins: out=xor_51_out
  and and_52 (and_52_out, xor_51_out, or_23_out);
  or or_23 (or_23_out, and_53_out, and_54_out);
  // XOR_Gate xor_52 has open pins: out=xor_52_out
  and and_53 (and_53_out, undriven_26, undriven_27);
  // XOR_Gate xor_53 has open pins: out=xor_53_out
  and and_54 (and_54_out, xor_53_out, or_24_out);
  or or_24 (or_24_out, and_55_out, and_56_out);
  // XOR_Gate xor_54 has open pins: out=xor_54_out
  and and_55 (and_55_out, undriven_28, undriven_29);
  // XOR_Gate xor_55 has open pins: out=xor_55_out
  and and_56 (and_56_out, xor_55_out, undriven_30);
  // XOR_Gate xor_56 has open pins: out=xor_56_out
  and and_57 (and_57_out, in_52, in_58);
  and and_58 (and_58_out, in_53, in_59);
  and and_59 (and_59_out, in_52, in_59);
  and and_60 (and_60_out, in_53, in_58);
  and and_61 (and_61_out, in_54, in_58);
  and and_62 (and_62_out, in_53, in_57);
  and and_63 (and_63_out, in_52, in_57);
  and and_64 (and_64_out, in_53, in_56);
  and and_65 (and_65_out, in_52, in_56);
  and and_66 (and_66_out, in_54, in_59);
  and and_67 (and_67_out, in_55, in_58);
  and and_68 (and_68_out, in_54, in_57);
  and and_69 (and_69_out, in_54, in_56);
  and and_70 (and_70_out, in_55, in_59);
  and and_71 (and_71_out, in_55, in_57);
  and and_72 (and_72_out, in_55, in_56);
endmodule
