// Logisim project lookaheadCarryAdderSubtractorWithoutOverflow.circ as structural Verilog: 6 circuits, main circuit main
module main (
);

  lookaheadAdderSubtractor lookaheadaddersubtractor_1 ();  // open: M, S0, S1, S2, S3, S4, S5, S6, S7, in_16, A7, A6, A5, A4, A3, A2, A1, B7, B6, B5, B4, B3, B2, B1, B0, V, Sign
endmodule

module lookaheadAdderSubtractor (
  input  A1,
  input  A2,
  input  A3,
  input  A4,
  input  A5,
  input  A6,
  input  B7,
  input  B6,
  input  B5,
  input  B4,
  input  B3,
  input  B2,
  input  B1,
  input  B0,
  input  A7,
  input  in_16,
  input  M,
  output S0,
  output S1,
  output S2,
  output S3,
  output S4,
  output S5,
  output S6,
  output S7,
  output V,
  output Sign
);

  wire and_1_out, and_2_out, and_3_out, and_4_out, and_5_out, and_6_out, and_7_out, and_8_out, and_9_out,
       and_10_out, and_11_out, and_12_out, and_13_out, and_14_out, and_15_out, and_16_out, and_17_out,
       and_18_out, and_19_out, and_20_out, and_21_out, and_22_out, and_23_out, and_24_out, and_25_out,
       and_26_out, and_27_out, and_28_out, and_29_out, and_30_out, and_31_out, and_32_out, and_33_out,
       and_34_out, and_35_out, and_36_out, and_37_out, and_38_out, or_1_out, or_2_out, or_3_out, or_4_out,
       or_5_out, or_6_out, or_7_out, or_8_out, or_9_out, or_10_out, or_11_out, or_12_out, xor_1_out,
       xor_2_out, xor_3_out, xor_4_out, xor_5_out, xor_6_out, xor_7_out, xor_8_out, xor_9_out, xor_10_out,
       xor_11_out, xor_12_out, xor_13_out, xor_14_out, xor_15_out, xor_16_out, xor_17_out, xor_18_out,
       xor_19_out, xor_20_out, xor_21_out, xor_22_out, xor_23_out, xor_24_out, xor_26_out, xor_28_out;

  xor xor_1 (xor_1_out, or_3_out, or_1_out);
  xor xor_2 (xor_2_out, or_4_out, or_2_out);
  Multiplexer multiplexer_1 (.in0(xor_1_out), .in1(xor_2_out), .out(V), .sel(or_9_out), .en(1'b1));
  Multiplexer multiplexer_2 (.in0(or_1_out), .in1(or_2_out), .out(Sign), .sel(or_9_out), .en(1'b1));
  xor xor_3 (xor_3_out, B6, M);
  xor xor_4 (xor_4_out, B7, M);
  xor xor_5 (xor_5_out, B5, M);
  and and_1 (and_1_out, in_16, xor_4_out);
  xor xor_6 (xor_6_out, in_16, xor_4_out);
  and and_2 (and_2_out, 1'b0, xor_6_out, xor_18_out, xor_15_out, xor_12_out);
  or or_1 (or_1_out, and_1_out, and_2_out, and_4_out, and_7_out, and_6_out);
  and and_3 (and_3_out, 1'b1, xor_6_out, xor_18_out, xor_15_out, xor_12_out);
  or or_2 (or_2_out, and_1_out, and_3_out, and_5_out, and_9_out, and_8_out);
  xor xor_7 (xor_7_out, B4, M);
  xor xor_8 (xor_8_out, B3, M);
  and and_4 (and_4_out, and_22_out, xor_15_out, xor_6_out, xor_12_out);
  and and_5 (and_5_out, and_22_out, xor_15_out, xor_6_out, xor_12_out);
  xor xor_9 (xor_9_out, B2, M);
  xor xor_10 (xor_10_out, B1, M);
  and and_6 (and_6_out, and_10_out, xor_6_out);
  and and_7 (and_7_out, and_15_out, xor_6_out, xor_12_out);
  and and_8 (and_8_out, and_10_out, xor_6_out);
  and and_9 (and_9_out, and_15_out, xor_6_out, xor_12_out);
  xor xor_11 (xor_11_out, B0, M);
  and and_10 (and_10_out, A7, xor_3_out);
  or or_3 (or_3_out, and_10_out, and_11_out, and_12_out, and_16_out);
  or or_4 (or_4_out, and_10_out, and_13_out, and_14_out, and_17_out);
  xor xor_12 (xor_12_out, A7, xor_3_out);
  and and_11 (and_11_out, 1'b0, xor_12_out, xor_18_out, xor_15_out);
  and and_12 (and_12_out, xor_12_out, xor_15_out, and_22_out);
  xor xor_13 (xor_13_out, or_3_out, xor_6_out);
  and and_13 (and_13_out, 1'b1, xor_12_out, xor_18_out, xor_15_out);
  and and_14 (and_14_out, xor_12_out, xor_15_out, and_22_out);
  xor xor_14 (xor_14_out, or_4_out, xor_6_out);
  and and_15 (and_15_out, A6, xor_5_out);
  and and_16 (and_16_out, xor_12_out, and_15_out);
  and and_17 (and_17_out, xor_12_out, and_15_out);
  or or_5 (or_5_out, and_15_out, and_21_out, and_20_out);
  xor xor_15 (xor_15_out, A6, xor_5_out);
  and and_18 (and_18_out, xor_15_out, and_22_out);
  and and_19 (and_19_out, 1'b0, xor_15_out, xor_18_out);
  or or_6 (or_6_out, and_15_out, and_19_out, and_18_out);
  xor xor_16 (xor_16_out, or_6_out, xor_12_out);
  and and_20 (and_20_out, xor_15_out, and_22_out);
  and and_21 (and_21_out, 1'b1, xor_15_out, xor_18_out);
  xor xor_17 (xor_17_out, or_5_out, xor_12_out);
  and and_22 (and_22_out, A5, xor_7_out);
  or or_7 (or_7_out, and_22_out, and_23_out);
  or or_8 (or_8_out, and_22_out, and_24_out);
  xor xor_18 (xor_18_out, A5, xor_7_out);
  and and_23 (and_23_out, xor_18_out, 1'b0);
  xor xor_19 (xor_19_out, or_7_out, xor_15_out);
  and and_24 (and_24_out, xor_18_out, 1'b1);
  xor xor_20 (xor_20_out, or_8_out, xor_15_out);
  xor xor_21 (xor_21_out, xor_18_out, 1'b0);
  xor xor_22 (xor_22_out, xor_18_out, 1'b1);
  xor xor_23 (xor_23_out, A4, xor_8_out);
  and and_25 (and_25_out, A4, xor_8_out);
  and and_26 (and_26_out, M, xor_23_out, xor_28_out, xor_26_out, xor_24_out);
  or or_9 (or_9_out, and_25_out, and_26_out, and_27_out, and_28_out, and_29_out);
  Multiplexer multiplexer_3 (.in0(xor_21_out), .in1(xor_22_out), .out(S4), .sel(or_9_out), .en(1'b1));
  Multiplexer multiplexer_4 (.in0(xor_19_out), .in1(xor_20_out), .out(S5), .sel(or_9_out), .en(1'b1));
  Multiplexer multiplexer_5 (.in0(xor_16_out), .in1(xor_17_out), .out(S6), .sel(or_9_out), .en(1'b1));
  Multiplexer multiplexer_6 (.in0(xor_13_out), .in1(xor_14_out), .out(S7), .sel(or_9_out), .en(1'b1));
  and and_27 (and_27_out, and_36_out, xor_26_out, xor_23_out, xor_24_out);
  and and_28 (and_28_out, and_34_out, xor_23_out, xor_24_out);
  and and_29 (and_29_out, and_30_out, xor_23_out);
  and and_30 (and_30_out, A3, xor_9_out);
  xor xor_24 (xor_24_out, A3, xor_9_out);
  and and_31 (and_31_out, M, xor_24_out, xor_28_out, xor_26_out);
  or or_10 (or_10_out, and_30_out, and_31_out, and_32_out, and_33_out);
  xor xor_25 (S3, or_10_out, xor_23_out);
  and and_32 (and_32_out, xor_24_out, xor_26_out, and_36_out);
  and and_33 (and_33_out, xor_24_out, and_34_out);
  xor xor_26 (xor_26_out, A2, xor_10_out);
  and and_34 (and_34_out, A2, xor_10_out);
  and and_35 (and_35_out, M, xor_26_out, xor_28_out);
  or or_11 (or_11_out, and_34_out, and_35_out, and_37_out);
  xor xor_27 (S2, or_11_out, xor_24_out);
  and and_36 (and_36_out, A1, xor_11_out);
  and and_37 (and_37_out, xor_26_out, and_36_out);
  or or_12 (or_12_out, and_36_out, and_38_out);
  xor xor_28 (xor_28_out, A1, xor_11_out);
  and and_38 (and_38_out, xor_28_out, M);
  xor xor_29 (S1, or_12_out, xor_26_out);
  xor xor_30 (S0, xor_28_out, M);

  // Notes on the sheet:
  //   A0
endmodule

module adder (
  input  A1,
  input  A2,
  input  A3,
  input  A4,
  input  A5,
  input  A6,
  input  A7,
  input  in_8,
  input  B7,
  input  B6,
  input  B5,
  input  B4,
  input  B3,
  input  B2,
  input  B1,
  input  B0,
  input  in_17,
  output S0,
  output S1,
  output S2,
  output S3,
  output S4,
  output S5,
  output S6,
  output S7,
  output V,
  output Sign
);

  wire and_1_out, and_2_out, and_3_out, and_4_out, and_5_out, and_6_out, and_7_out, and_8_out, and_9_out,
       and_10_out, and_11_out, and_12_out, and_13_out, and_14_out, and_15_out, and_16_out, and_17_out,
       and_18_out, and_19_out, and_20_out, and_21_out, and_22_out, and_23_out, and_24_out, and_25_out,
       and_26_out, and_27_out, and_28_out, and_29_out, and_30_out, and_31_out, and_32_out, and_33_out,
       and_34_out, and_35_out, and_36_out, and_37_out, and_38_out, or_1_out, or_2_out, or_3_out, or_4_out,
       or_5_out, or_6_out, or_7_out, or_8_out, or_9_out, or_10_out, or_11_out, or_12_out, xor_1_out,
       xor_2_out, xor_3_out, xor_4_out, xor_5_out, xor_6_out, xor_7_out, xor_8_out, xor_9_out, xor_10_out,
       xor_11_out, xor_12_out, xor_13_out, xor_14_out, xor_15_out, xor_16_out, xor_18_out, xor_20_out;

  xor xor_1 (xor_1_out, or_3_out, or_1_out);
  xor xor_2 (xor_2_out, or_4_out, or_2_out);
  Multiplexer multiplexer_1 (.in0(xor_1_out), .in1(xor_2_out), .out(V), .sel(or_9_out), .en(1'b1));
  Multiplexer multiplexer_2 (.in0(or_1_out), .in1(or_2_out), .out(Sign), .sel(or_9_out), .en(1'b1));
  xor xor_3 (xor_3_out, in_8, B7);
  and and_1 (and_1_out, in_8, B7);
  and and_2 (and_2_out, 1'b0, xor_3_out, xor_10_out, xor_7_out, xor_4_out);
  or or_1 (or_1_out, and_1_out, and_2_out, and_4_out, and_7_out, and_6_out);
  and and_3 (and_3_out, 1'b1, xor_3_out, xor_10_out, xor_7_out, xor_4_out);
  or or_2 (or_2_out, and_1_out, and_3_out, and_5_out, and_8_out, and_9_out);
  and and_4 (and_4_out, and_22_out, xor_7_out, xor_3_out, xor_4_out);
  and and_5 (and_5_out, and_22_out, xor_7_out, xor_3_out, xor_4_out);
  and and_6 (and_6_out, and_10_out, xor_3_out);
  and and_7 (and_7_out, and_15_out, xor_3_out, xor_4_out);
  and and_8 (and_8_out, and_15_out, xor_3_out, xor_4_out);
  and and_9 (and_9_out, and_10_out, xor_3_out);
  and and_10 (and_10_out, A7, B6);
  or or_3 (or_3_out, and_10_out, and_11_out, and_12_out, and_16_out);
  or or_4 (or_4_out, and_10_out, and_13_out, and_14_out, and_17_out);
  xor xor_4 (xor_4_out, A7, B6);
  and and_11 (and_11_out, 1'b0, xor_4_out, xor_10_out, xor_7_out);
  and and_12 (and_12_out, xor_4_out, xor_7_out, and_22_out);
  xor xor_5 (xor_5_out, or_3_out, xor_3_out);
  and and_13 (and_13_out, 1'b1, xor_4_out, xor_10_out, xor_7_out);
  and and_14 (and_14_out, xor_4_out, xor_7_out, and_22_out);
  xor xor_6 (xor_6_out, or_4_out, xor_3_out);
  and and_15 (and_15_out, A6, B5);
  and and_16 (and_16_out, xor_4_out, and_15_out);
  and and_17 (and_17_out, xor_4_out, and_15_out);
  or or_5 (or_5_out, and_15_out, and_21_out, and_20_out);
  xor xor_7 (xor_7_out, A6, B5);
  and and_18 (and_18_out, xor_7_out, and_22_out);
  and and_19 (and_19_out, 1'b0, xor_7_out, xor_10_out);
  or or_6 (or_6_out, and_15_out, and_19_out, and_18_out);
  xor xor_8 (xor_8_out, or_6_out, xor_4_out);
  and and_20 (and_20_out, xor_7_out, and_22_out);
  and and_21 (and_21_out, 1'b1, xor_7_out, xor_10_out);
  xor xor_9 (xor_9_out, or_5_out, xor_4_out);
  and and_22 (and_22_out, A5, B4);
  or or_7 (or_7_out, and_22_out, and_23_out);
  or or_8 (or_8_out, and_22_out, and_24_out);
  xor xor_10 (xor_10_out, A5, B4);
  and and_23 (and_23_out, xor_10_out, 1'b0);
  xor xor_11 (xor_11_out, or_7_out, xor_7_out);
  and and_24 (and_24_out, xor_10_out, 1'b1);
  xor xor_12 (xor_12_out, or_8_out, xor_7_out);
  xor xor_13 (xor_13_out, xor_10_out, 1'b0);
  xor xor_14 (xor_14_out, xor_10_out, 1'b1);
  xor xor_15 (xor_15_out, A4, B3);
  and and_25 (and_25_out, A4, B3);
  and and_26 (and_26_out, in_17, xor_15_out, xor_20_out, xor_18_out, xor_16_out);
  or or_9 (or_9_out, and_25_out, and_26_out, and_27_out, and_29_out, and_28_out);
  Multiplexer multiplexer_3 (.in0(xor_13_out), .in1(xor_14_out), .out(S4), .sel(or_9_out), .en(1'b1));
  Multiplexer multiplexer_4 (.in0(xor_11_out), .in1(xor_12_out), .out(S5), .sel(or_9_out), .en(1'b1));
  Multiplexer multiplexer_5 (.in0(xor_8_out), .in1(xor_9_out), .out(S6), .sel(or_9_out), .en(1'b1));
  Multiplexer multiplexer_6 (.in0(xor_5_out), .in1(xor_6_out), .out(S7), .sel(or_9_out), .en(1'b1));
  and and_27 (and_27_out, and_36_out, xor_18_out, xor_15_out, xor_16_out);
  and and_28 (and_28_out, and_30_out, xor_15_out);
  and and_29 (and_29_out, and_34_out, xor_15_out, xor_16_out);
  and and_30 (and_30_out, A3, B2);
  xor xor_16 (xor_16_out, A3, B2);
  and and_31 (and_31_out, in_17, xor_16_out, xor_20_out, xor_18_out);
  or or_10 (or_10_out, and_30_out, and_31_out, and_32_out, and_33_out);
  xor xor_17 (S3, or_10_out, xor_15_out);
  and and_32 (and_32_out, xor_16_out, xor_18_out, and_36_out);
  and and_33 (and_33_out, xor_16_out, and_34_out);
  xor xor_18 (xor_18_out, A2, B1);
  and and_34 (and_34_out, A2, B1);
  and and_35 (and_35_out, in_17, xor_18_out, xor_20_out);
  or or_11 (or_11_out, and_34_out, and_35_out, and_37_out);
  xor xor_19 (S2, or_11_out, xor_16_out);
  and and_36 (and_36_out, A1, B0);
  and and_37 (and_37_out, xor_18_out, and_36_out);
  or or_12 (or_12_out, and_36_out, and_38_out);
  xor xor_20 (xor_20_out, A1, B0);
  and and_38 (and_38_out, xor_20_out, in_17);
  xor xor_21 (S1, or_12_out, xor_18_out);
  xor xor_22 (S0, xor_20_out, in_17);

  // Notes on the sheet:
  //   A0
  //   M
endmodule

module Multiplier (
  input  in_1,
  input  in_2,
  input  in_3,
  input  in_4,
  input  in_5,
  input  in_6,
  input  in_7,
  input  in_8,
  input  in_9,
  input  in_10,
  input  in_11,
  input  in_12,
  input  in_13,
  input  in_14,
  input  in_15,
  input  in_16,
  output out_17,
  output out_18,
  output out_19,
  output out_20,
  output out_21,
  output out_22,
  output out_23,
  output out_24,
  output out_25,
  output out_26,
  output out_27,
  output out_28,
  output out_29,
  output out_30,
  output out_31,
  output out_32
);

  wire adder_1_s1, adder_1_s2, adder_1_s3, adder_1_s4, adder_1_s5, adder_1_s6, adder_1_s7, adder_1_sign,
       adder_2_s1, adder_2_s2, adder_2_s3, adder_2_s4, adder_2_s5, adder_2_s6, adder_2_s7, adder_2_sign,
       adder_3_s1, adder_3_s2, adder_3_s3, adder_3_s4, adder_3_s5, adder_3_s6, adder_3_s7, adder_3_sign,
       adder_4_s1, adder_4_s2, adder_4_s3, adder_4_s4, adder_4_s5, adder_4_s6, adder_4_s7, adder_4_sign,
       adder_5_s1, adder_5_s2, adder_5_s3, adder_5_s4, adder_5_s5, adder_5_s6, adder_5_s7, adder_5_sign,
       adder_6_s1, adder_6_s2, adder_6_s3, adder_6_s4, adder_6_s5, adder_6_s6, adder_6_s7, adder_6_sign,
       and8x1_1_out_10, and8x1_1_out_11, and8x1_1_out_12, and8x1_1_out_13, and8x1_1_out_14, and8x1_1_out_15,
       and8x1_1_out_16, and8x1_2_out_10, and8x1_2_out_11, and8x1_2_out_12, and8x1_2_out_13, and8x1_2_out_14,
       and8x1_2_out_15, and8x1_2_out_16, and8x1_2_out_17, and8x1_3_out_10, and8x1_3_out_11, and8x1_3_out_12,
       and8x1_3_out_13, and8x1_3_out_14, and8x1_3_out_15, and8x1_3_out_16, and8x1_3_out_17, and8x1_4_out_10,
       and8x1_4_out_11, and8x1_4_out_12, and8x1_4_out_13, and8x1_4_out_14, and8x1_4_out_15, and8x1_4_out_16,
       and8x1_4_out_17, and8x1_5_out_10, and8x1_5_out_11, and8x1_5_out_12, and8x1_5_out_13, and8x1_5_out_14,
       and8x1_5_out_15, and8x1_5_out_16, and8x1_5_out_17, and8x1_6_out_10, and8x1_6_out_11, and8x1_6_out_12,
       and8x1_6_out_13, and8x1_6_out_14, and8x1_6_out_15, and8x1_6_out_16, and8x1_6_out_17, and8x1_7_out_10,
       and8x1_7_out_11, and8x1_7_out_12, and8x1_7_out_13, and8x1_7_out_14, and8x1_7_out_15, and8x1_7_out_16,
       and8x1_7_out_17, and8x1_8_out_10, and8x1_8_out_11, and8x1_8_out_12, and8x1_8_out_13, and8x1_8_out_14,
       and8x1_8_out_15, and8x1_8_out_16, and8x1_8_out_17;

  And8x1 and8x1_1 (
    .in_1(in_1), .in_2(in_2), .in_3(in_3), .in_4(in_4), .in_5(in_5), .in_6(in_6), .in_7(in_7), .in_8(in_8),
    .out_10(and8x1_1_out_10), .out_11(and8x1_1_out_11), .out_12(and8x1_1_out_12), .out_13(and8x1_1_out_13),
    .out_14(and8x1_1_out_14), .out_15(and8x1_1_out_15), .out_16(and8x1_1_out_16), .out_17(out_17),
    .in_9(in_16));
  adder adder_1 (
    .S0(out_18), .S1(adder_1_s1), .S2(adder_1_s2), .S3(adder_1_s3), .S4(adder_1_s4), .S5(adder_1_s5),
    .S6(adder_1_s6), .S7(adder_1_s7), .in_8(1'b0), .A7(and8x1_1_out_10), .A6(and8x1_1_out_11),
    .A5(and8x1_1_out_12), .A4(and8x1_1_out_13), .A3(and8x1_1_out_14), .A2(and8x1_1_out_15),
    .A1(and8x1_1_out_16), .B7(and8x1_2_out_10), .B6(and8x1_2_out_11), .B5(and8x1_2_out_12),
    .B4(and8x1_2_out_13), .B3(and8x1_2_out_14), .B2(and8x1_2_out_15), .B1(and8x1_2_out_16),
    .B0(and8x1_2_out_17), .Sign(adder_1_sign), .in_17(1'b0));  // open: V
  And8x1 and8x1_2 (
    .in_1(in_1), .in_2(in_2), .in_3(in_3), .in_4(in_4), .in_5(in_5), .in_6(in_6), .in_7(in_7), .in_8(in_8),
    .out_10(and8x1_2_out_10), .out_11(and8x1_2_out_11), .out_12(and8x1_2_out_12), .out_13(and8x1_2_out_13),
    .out_14(and8x1_2_out_14), .out_15(and8x1_2_out_15), .out_16(and8x1_2_out_16), .out_17(and8x1_2_out_17),
    .in_9(in_15));
  adder adder_2 (
    .S0(out_19), .S1(adder_2_s1), .S2(adder_2_s2), .S3(adder_2_s3), .S4(adder_2_s4), .S5(adder_2_s5),
    .S6(adder_2_s6), .S7(adder_2_s7), .in_8(adder_1_sign), .A7(adder_1_s7), .A6(adder_1_s6), .A5(adder_1_s5),
    .A4(adder_1_s4), .A3(adder_1_s3), .A2(adder_1_s2), .A1(adder_1_s1), .B7(and8x1_3_out_10),
    .B6(and8x1_3_out_11), .B5(and8x1_3_out_12), .B4(and8x1_3_out_13), .B3(and8x1_3_out_14),
    .B2(and8x1_3_out_15), .B1(and8x1_3_out_16), .B0(and8x1_3_out_17), .Sign(adder_2_sign), .in_17(1'b0));  // open: V
  And8x1 and8x1_3 (
    .in_1(in_1), .in_2(in_2), .in_3(in_3), .in_4(in_4), .in_5(in_5), .in_6(in_6), .in_7(in_7), .in_8(in_8),
    .out_10(and8x1_3_out_10), .out_11(and8x1_3_out_11), .out_12(and8x1_3_out_12), .out_13(and8x1_3_out_13),
    .out_14(and8x1_3_out_14), .out_15(and8x1_3_out_15), .out_16(and8x1_3_out_16), .out_17(and8x1_3_out_17),
    .in_9(in_14));
  adder adder_3 (
    .S0(out_20), .S1(adder_3_s1), .S2(adder_3_s2), .S3(adder_3_s3), .S4(adder_3_s4), .S5(adder_3_s5),
    .S6(adder_3_s6), .S7(adder_3_s7), .in_8(adder_2_sign), .A7(adder_2_s7), .A6(adder_2_s6), .A5(adder_2_s5),
    .A4(adder_2_s4), .A3(adder_2_s3), .A2(adder_2_s2), .A1(adder_2_s1), .B7(and8x1_4_out_10),
    .B6(and8x1_4_out_11), .B5(and8x1_4_out_12), .B4(and8x1_4_out_13), .B3(and8x1_4_out_14),
    .B2(and8x1_4_out_15), .B1(and8x1_4_out_16), .B0(and8x1_4_out_17), .Sign(adder_3_sign), .in_17(1'b0));  // open: V
  And8x1 and8x1_4 (
    .in_1(in_1), .in_2(in_2), .in_3(in_3), .in_4(in_4), .in_5(in_5), .in_6(in_6), .in_7(in_7), .in_8(in_8),
    .out_10(and8x1_4_out_10), .out_11(and8x1_4_out_11), .out_12(and8x1_4_out_12), .out_13(and8x1_4_out_13),
    .out_14(and8x1_4_out_14), .out_15(and8x1_4_out_15), .out_16(and8x1_4_out_16), .out_17(and8x1_4_out_17),
    .in_9(in_13));
  adder adder_4 (
    .S0(out_21), .S1(adder_4_s1), .S2(adder_4_s2), .S3(adder_4_s3), .S4(adder_4_s4), .S5(adder_4_s5),
    .S6(adder_4_s6), .S7(adder_4_s7), .in_8(adder_3_sign), .A7(adder_3_s7), .A6(adder_3_s6), .A5(adder_3_s5),
    .A4(adder_3_s4), .A3(adder_3_s3), .A2(adder_3_s2), .A1(adder_3_s1), .B7(and8x1_5_out_10),
    .B6(and8x1_5_out_11), .B5(and8x1_5_out_12), .B4(and8x1_5_out_13), .B3(and8x1_5_out_14),
    .B2(and8x1_5_out_15), .B1(and8x1_5_out_16), .B0(and8x1_5_out_17), .Sign(adder_4_sign), .in_17(1'b0));  // open: V
  adder adder_5 (
    .S0(out_22), .S1(adder_5_s1), .S2(adder_5_s2), .S3(adder_5_s3), .S4(adder_5_s4), .S5(adder_5_s5),
    .S6(adder_5_s6), .S7(adder_5_s7), .in_8(adder_4_sign), .A7(adder_4_s7), .A6(adder_4_s6), .A5(adder_4_s5),
    .A4(adder_4_s4), .A3(adder_4_s3), .A2(adder_4_s2), .A1(adder_4_s1), .B7(and8x1_6_out_10),
    .B6(and8x1_6_out_11), .B5(and8x1_6_out_12), .B4(and8x1_6_out_13), .B3(and8x1_6_out_14),
    .B2(and8x1_6_out_15), .B1(and8x1_6_out_16), .B0(and8x1_6_out_17), .Sign(adder_5_sign), .in_17(1'b0));  // open: V
  And8x1 and8x1_5 (
    .in_1(in_1), .in_2(in_2), .in_3(in_3), .in_4(in_4), .in_5(in_5), .in_6(in_6), .in_7(in_7), .in_8(in_8),
    .out_10(and8x1_5_out_10), .out_11(and8x1_5_out_11), .out_12(and8x1_5_out_12), .out_13(and8x1_5_out_13),
    .out_14(and8x1_5_out_14), .out_15(and8x1_5_out_15), .out_16(and8x1_5_out_16), .out_17(and8x1_5_out_17),
    .in_9(in_12));
  adder adder_6 (
    .S0(out_23), .S1(adder_6_s1), .S2(adder_6_s2), .S3(adder_6_s3), .S4(adder_6_s4), .S5(adder_6_s5),
    .S6(adder_6_s6), .S7(adder_6_s7), .in_8(adder_5_sign), .A7(adder_5_s7), .A6(adder_5_s6), .A5(adder_5_s5),
    .A4(adder_5_s4), .A3(adder_5_s3), .A2(adder_5_s2), .A1(adder_5_s1), .B7(and8x1_7_out_10),
    .B6(and8x1_7_out_11), .B5(and8x1_7_out_12), .B4(and8x1_7_out_13), .B3(and8x1_7_out_14),
    .B2(and8x1_7_out_15), .B1(and8x1_7_out_16), .B0(and8x1_7_out_17), .Sign(adder_6_sign), .in_17(1'b0));  // open: V
  And8x1 and8x1_6 (
    .in_1(in_1), .in_2(in_2), .in_3(in_3), .in_4(in_4), .in_5(in_5), .in_6(in_6), .in_7(in_7), .in_8(in_8),
    .out_10(and8x1_6_out_10), .out_11(and8x1_6_out_11), .out_12(and8x1_6_out_12), .out_13(and8x1_6_out_13),
    .out_14(and8x1_6_out_14), .out_15(and8x1_6_out_15), .out_16(and8x1_6_out_16), .out_17(and8x1_6_out_17),
    .in_9(in_11));
  And8x1 and8x1_7 (
    .in_1(in_1), .in_2(in_2), .in_3(in_3), .in_4(in_4), .in_5(in_5), .in_6(in_6), .in_7(in_7), .in_8(in_8),
    .out_10(and8x1_7_out_10), .out_11(and8x1_7_out_11), .out_12(and8x1_7_out_12), .out_13(and8x1_7_out_13),
    .out_14(and8x1_7_out_14), .out_15(and8x1_7_out_15), .out_16(and8x1_7_out_16), .out_17(and8x1_7_out_17),
    .in_9(in_10));
  adder adder_7 (
    .S0(out_24), .S1(out_25), .S2(out_26), .S3(out_27), .S4(out_28), .S5(out_29), .S6(out_30), .S7(out_31),
    .in_8(adder_6_sign), .A7(adder_6_s7), .A6(adder_6_s6), .A5(adder_6_s5), .A4(adder_6_s4), .A3(adder_6_s3),
    .A2(adder_6_s2), .A1(adder_6_s1), .B7(and8x1_8_out_10), .B6(and8x1_8_out_11), .B5(and8x1_8_out_12),
    .B4(and8x1_8_out_13), .B3(and8x1_8_out_14), .B2(and8x1_8_out_15), .B1(and8x1_8_out_16),
    .B0(and8x1_8_out_17), .Sign(out_32), .in_17(1'b0));  // open: V
  And8x1 and8x1_8 (
    .in_1(in_1), .in_2(in_2), .in_3(in_3), .in_4(in_4), .in_5(in_5), .in_6(in_6), .in_7(in_7), .in_8(in_8),
    .out_10(and8x1_8_out_10), .out_11(and8x1_8_out_11), .out_12(and8x1_8_out_12), .out_13(and8x1_8_out_13),
    .out_14(and8x1_8_out_14), .out_15(and8x1_8_out_15), .out_16(and8x1_8_out_16), .out_17(and8x1_8_out_17),
    .in_9(in_9));

  // Other names for the same wires on the sheet: A0 = in_8; A1 = in_7; A2 = in_6; A3 = in_5; A4 = in_4; A5 = in_3;
  //   A6 = in_2; A7 = in_1; B0 = in_16; B1 = in_15; B2 = in_14; B3 = in_13; B4 = in_12; B5 = in_11; B6 = in_10;
  //   B7 = in_9
endmodule

module And8x1 (
  input  in_1,
  input  in_2,
  input  in_3,
  input  in_4,
  input  in_5,
  input  in_6,
  input  in_7,
  input  in_8,
  input  in_9,
  output out_10,
  output out_11,
  output out_12,
  output out_13,
  output out_14,
  output out_15,
  output out_16,
  output out_17
);

  and and_1 (out_10, in_1, in_9);
  and and_2 (out_11, in_2, in_9);
  and and_3 (out_13, in_4, in_9);
  and and_4 (out_12, in_3, in_9);
  and and_5 (out_15, in_6, in_9);
  and and_6 (out_14, in_5, in_9);
  and and_7 (out_16, in_7, in_9);
  and and_8 (out_17, in_8, in_9);
endmodule

module _4bitAdder (
  input  in_1,
  input  in_2,
  input  in_3,
  input  in_4,
  output S0,
  output S1,
  output S2,
  output S3
);

  wire and_1_out, and_2_out, and_3_out, and_4_out, and_5_out, or_1_out, or_2_out, xor_2_out;

  or or_1 (or_1_out, and_1_out, and_3_out);
  and and_1 (and_1_out, in_2, xor_2_out, and_5_out);
  xor xor_1 (S3, or_1_out, in_1);
  and and_2 (and_2_out, 1'b1, in_3);
  and and_3 (and_3_out, in_2, and_2_out);
  or or_2 (or_2_out, and_2_out, and_4_out);
  xor xor_2 (xor_2_out, 1'b1, in_3);
  and and_4 (and_4_out, xor_2_out, and_5_out);
  xor xor_3 (S2, or_2_out, in_2);
  xor xor_4 (S0, 1'b1, in_4);
  and and_5 (and_5_out, 1'b1, in_4);
  xor xor_5 (S1, and_5_out, xor_2_out);
endmodule
