// Logisim project rough.circ as structural Verilog
module leftShiftRegister (
  input  in_1,
  input  in_2,
  input  in_3,
  input  in_4,
  input  in_5,
  input  in_6,
  input  in_7,
  input  in_8,
  input  in_9,
  input  in_10,
  input  in_11,
  input  in_12,
  input  in_13,
  input  in_14,
  input  in_15,
  input  in_16,
  input  in_17,
  input  in_18
);

  wire clock_1_out, shift_register_1_out, shift_register_2_q7;
  wire [7:0] adder_1_out, and_1_out, shift_register_1_q7, shift_register_1_q15;

  Clock clock_1 (.out(clock_1_out));
  Shift_Register #(.length(16)) shift_register_1 (
    .in(shift_register_1_out), .clk(clock_1_out), .out(shift_register_1_out), .load(shift_register_2_q7),
    .clr(in_1), .d0(adder_1_out[7]), .q0(shift_register_1_q7[7]), .d1(adder_1_out[6]),
    .q1(shift_register_1_q7[6]), .d2(adder_1_out[5]), .q2(shift_register_1_q7[5]), .d3(adder_1_out[4]),
    .q3(shift_register_1_q7[4]), .d4(adder_1_out[3]), .q4(shift_register_1_q7[3]), .d5(adder_1_out[2]),
    .q5(shift_register_1_q7[2]), .d6(adder_1_out[1]), .q6(shift_register_1_q7[1]), .d7(adder_1_out[0]),
    .q7(shift_register_1_q7[0]), .d8(shift_register_1_q15[7]), .q8(shift_register_1_q15[7]),
    .d9(shift_register_1_q15[6]), .q9(shift_register_1_q15[6]), .d10(shift_register_1_q15[5]),
    .q10(shift_register_1_q15[5]), .d11(shift_register_1_q15[4]), .q11(shift_register_1_q15[4]),
    .d12(shift_register_1_q15[3]), .q12(shift_register_1_q15[3]), .d13(shift_register_1_q15[2]),
    .q13(shift_register_1_q15[2]), .d14(shift_register_1_q15[1]), .q14(shift_register_1_q15[1]),
    .d15(shift_register_1_q15[0]), .q15(shift_register_1_q15[0]));  // open: shift
  Shift_Register shift_register_2 (
    .clk(clock_1_out), .load(in_7), .d0(in_2), .d1(in_4), .d2(in_5), .d3(in_8), .d4(in_9), .d5(in_11),
    .d6(in_12), .d7(in_14), .q7(shift_register_2_q7));  // open: shift, in, out, clr, q0, q1, q2, q3, q4, q5, q6
  Adder adder_1 (.a(shift_register_1_q7), .b(and_1_out), .out(adder_1_out));  // open: cin, cout
  and and_1 (and_1_out[0], in_3, shift_register_2_q7);
  and and_2 (and_1_out[1], in_6, shift_register_2_q7);
  and and_3 (and_1_out[2], in_10, shift_register_2_q7);
  and and_4 (and_1_out[3], in_13, shift_register_2_q7);
  and and_5 (and_1_out[4], in_15, shift_register_2_q7);
  and and_6 (and_1_out[5], in_16, shift_register_2_q7);
  and and_7 (and_1_out[6], in_17, shift_register_2_q7);
  and and_8 (and_1_out[7], in_18, shift_register_2_q7);
endmodule
